// Logisim project NSU-2023-T05L2e05.circ as structural Verilog: 2 circuits, main circuit bcd2
module bcd2 (
  input  Cin,
  input  [7:0] A,
  input  [7:0] B,
  output [7:0] R,
  output Cout
);

  wire bcd_add_1_cout;

  Hex_Digit_Display hex_digit_display_1 (.value(A[7:4]));  // open: dp
  Hex_Digit_Display hex_digit_display_2 (.value(B[7:4]));  // open: dp
  Hex_Digit_Display hex_digit_display_3 (.value({3'b000, Cin}));  // open: dp
  Hex_Digit_Display hex_digit_display_4 (.value(A[3:0]));  // open: dp
  Hex_Digit_Display hex_digit_display_5 (.value(B[3:0]));  // open: dp
  bcd_add bcd_add_1 (.Cin(Cin), .A(A[3:0]), .B(B[3:0]), .A_2(R[3:0]), .Cout(bcd_add_1_cout));
  bcd_add bcd_add_2 (.Cin(bcd_add_1_cout), .A(A[7:4]), .B(B[7:4]), .A_2(R[7:4]), .Cout(Cout));
  Hex_Digit_Display hex_digit_display_6 (.value({3'b000, Cout}));  // open: dp
  Hex_Digit_Display hex_digit_display_7 (.value(R[7:4]));  // open: dp
  Hex_Digit_Display hex_digit_display_8 (.value(R[3:0]));  // open: dp
endmodule

// BCD
module bcd_add (
  input  Cin,
  input  [3:0] A,
  input  [3:0] B,
  output [3:0] A_2,
  output Cout
);

  wire and_1_out, \bit , or_1_out, sum1_1_cout, sum1_2_cout, sum1_3_cout, sum4_1_cout;
  wire [3:0] and_2_out, sum1_1_out;
  wire [3:3] or_2_out;

  Sum1 sum1_1 (.in(A[0]), .in_2(B[0]), .Cin(Cin), .Cout(sum1_1_cout), .Out(sum1_1_out[0]));
  Sum1 sum1_2 (.in(A[1]), .in_2(B[1]), .Cin(sum1_1_cout), .Cout(sum1_2_cout), .Out(sum1_1_out[1]));
  Sum1 sum1_3 (.in(A[2]), .in_2(B[2]), .Cin(sum1_2_cout), .Cout(sum1_3_cout), .Out(sum1_1_out[2]));
  Sum1 sum1_4 (.in(A[3]), .in_2(B[3]), .Cin(sum1_3_cout), .Cout(\bit ), .Out(sum1_1_out[3]));
  or or_1 (or_1_out, sum1_1_out[2], sum1_1_out[1]);
  and and_1 (and_1_out, sum1_1_out[3], or_1_out);
  or or_2 (or_2_out[3], and_1_out, \bit );
  Sum4 sum4_1 (.Out(A_2), .Cout(sum4_1_cout), .in1(and_2_out), .in2(sum1_1_out));
  assign and_2_out = {4{or_2_out[3]}} & 4'b0110;  // AND_Gate and_2, 4 bits wide
  or or_3 (Cout, sum4_1_cout, \bit );
endmodule
