// Logisim project NSU-2023-T05L3e01.circ as structural Verilog: 2 circuits, main circuit ALU
module ALU (
  input  Cin,
  input  [7:0] A,
  input  [7:0] B,
  input  [1:0] instr,
  output V,
  output Cout,
  output [7:0] R
);

  wire and_1_out, subtractor_1_bout, sum8_1_cout, sumv_1_out_3;
  wire [7:0] and_2_out, or_1_out, r_t, sum8_1_out;

  // Probe on A
  // Probe on B
  SUMV sumv_1 (.in_1(A[7]), .in_2(B[7]), .out_3(sumv_1_out_3));
  and and_1 (and_1_out, B[7], r_t[7]);
  Sum8 sum8_1 (.Out(sum8_1_out), .Cout(sum8_1_cout), .in1(A), .in2(B), .Cin(Cin));
  assign and_2_out = A & B;  // AND_Gate and_2, 8 bits wide
  assign or_1_out = A | B;  // OR_Gate or_1, 8 bits wide
  Subtractor subtractor_1 (.a(A), .b(B), .out(r_t), .bin(Cin), .bout(subtractor_1_bout));
  Multiplexer #(.select(2), .enable("false")) multiplexer_1 (
    .in0(1'b0), .in1(1'b0), .in2(sumv_1_out_3), .in3(and_1_out), .out(V), .sel(instr));
  Multiplexer #(.select(2), .enable("false")) multiplexer_2 (
    .in0(1'b0), .in1(1'b0), .in2(sum8_1_cout), .in3(subtractor_1_bout), .out(Cout), .sel(instr));
  Multiplexer #(.select(2), .width(8), .enable("false")) multiplexer_3 (
    .in0(and_2_out), .in1(or_1_out), .in2(sum8_1_out), .in3(r_t), .out(R), .sel(instr));
  // Probe on R

  // Notes on the sheet:
  //   00: and
  //   01: or
  //   10: add
  //   11: sub
endmodule

module SUMV (
  input  in_1,
  input  in_2,
  output out_3
);

  wire xnor_1_out, xor_1_out;

  xor xor_1 (xor_1_out, in_1, in_2);
  and and_1 (out_3, xor_1_out, xnor_1_out);
  xnor xnor_1 (xnor_1_out, in_1, in_2);

  // Notes on the sheet:
  //   NOT(A7 XOR B7) AND (A7 XOR R7) 
endmodule
