// Logisim project NSU-2023-T06L1e01.circ as structural Verilog: 1 circuit, main circuit fib32
module fib32 (
  input  clock,
  output [31:0] a,
  output [5:0] k,
  output stop
);

  wire or_1_out;
  wire [31:0] multiplexer_1_out, register_1_q, register_2_q;

  Register #(.width(32)) register_1 (.D(register_2_q), .Q(register_1_q), .clk(clock));  // open: en, clr
  Register #(.width(32)) register_2 (.D(a), .Q(register_2_q), .clk(clock));  // open: en, clr
  Multiplexer #(.width(32), .enable("false")) multiplexer_1 (
    .in0(32'h1), .in1(register_1_q), .out(multiplexer_1_out), .sel(or_1_out));
  or or_1 (or_1_out, k[5], k[4], k[3], k[2], k[1], k[0]);
  // Probe on a
  Adder #(.width(32)) adder_1 (.a(multiplexer_1_out), .b(register_2_q), .out(a), .cout(stop));  // open: cin
  Counter #(.width(6), .max('h3f), .ongoal("stay")) counter_1 (.Q(k), .clk(clock));  // open: load, D, count, carry, clr
  // Probe on k
endmodule
