// Logisim project Adresses.circ as structural Verilog: 8 circuits, main circuit 1
module _0 (
  input  clock,
  input  [3:0] adr,
  output out
);

  and and_1 (out, clock, ~adr[3], adr[2], adr[1], adr[0]);  // AND_Gate
endmodule

module _1 (
  input  clock,
  input  [3:0] adr,
  output out
);

  and and_1 (out, clock, ~adr[3], adr[2], adr[1], ~adr[0]);  // AND_Gate
endmodule

module _2 (
  input  clock,
  input  [3:0] adr,
  output out
);

  and and_1 (out, clock, ~adr[3], adr[2], ~adr[1], adr[0]);  // AND_Gate
endmodule

module _3 (
  input  clock,
  input  [3:0] adr,
  output out
);

  and and_1 (out, clock, ~adr[3], adr[2], ~adr[1], ~adr[0]);  // AND_Gate
endmodule

module _4 (
  input  clock,
  input  [3:0] adr,
  output out
);

  and and_1 (out, clock, ~adr[3], ~adr[2], adr[1], adr[0]);  // AND_Gate
endmodule

module _5 (
  input  clock,
  input  [3:0] adr,
  output out
);

  and and_1 (out, clock, ~adr[3], ~adr[2], adr[1], ~adr[0]);  // AND_Gate
endmodule

module _6 (
  input  clock,
  input  [3:0] adr,
  output out
);

  and and_1 (out, clock, ~adr[3], ~adr[2], ~adr[1], adr[0]);  // AND_Gate
endmodule

module _7 (
  input  clock,
  input  [3:0] adr,
  output out
);

  and and_1 (out, clock, ~adr[3], ~adr[2], ~adr[1], ~adr[0]);  // AND_Gate
endmodule
