// Logisim project CSProject 3.09b.circ as structural Verilog: 6 circuits, main circuit main
module main (
  input  [7:0] bus_0,
  input  bus_0_2,
  output halted
);

  wire and_1_out, and_2_out, and_3_out, and_4_out, and_5_out, and_6_out, and_7_out, and_8_out, and_9_out,
       btA, btB, btC, btD, btE, btF, btG, btH, btI, btJ, btK, btL, btM, btN, btO, btP, btQ, btR, btS, btT,
       btU, btV, btW, btX, btY, btZ, button_1_out, cdm_8_mark5_1_p4, cdm_8_mark5_1_p6, cdm_8_mark5_1_p7,
       cdm_8_mark5_1_p8, cdm_8_mark5_1_p9, cdm_8_mark5_1_p10, cdm_8_mark5_1_p11, cl, clock_1_out, code,
       counter_1_carry, data, kcl, life_cntr_1_game_over, not_1_out, pull_resistor_3_node,
       pull_resistor_4_node, rd_wr, transistor_1_out, transistor_8_out, transistor_23_out;
  wire [2:0] adr;
  wire [3:0] counter_invertor_1_output, life_cntr_1_display;
  wire [4:0] bt, \let , random_1_out, register_1_q;
  wire [7:0] adder_1_out, cdm_8_mark5_1_p3, cdm_8_mark5_1_p13, cdm_8_mark5_1_p14, cdm_8_mark5_1_p15,
       controlled_buffer_1_out, r0, rom_2_data, transistor_17_out;
  wire [7:5] ram_2_data;
  wire [8:0] switch_3_0_1_output, switch_3_0_1_output_2, switch_3_0_1_output_3, switch_3_0_1_output_4,
       switch_3_0_1_output_5, switch_3_0_1_output_6, switch_3_0_1_output_7, switch_3_0_1_output_8,
       switch_3_0_1_output_9, switch_3_0_2_output, switch_3_0_2_output_2, switch_3_0_2_output_3,
       switch_3_0_2_output_4, switch_3_0_2_output_5, switch_3_0_2_output_6, switch_3_0_2_output_7,
       switch_3_0_2_output_8, switch_3_0_2_output_9, switch_3_0_3_output, switch_3_0_3_output_2,
       switch_3_0_3_output_3, switch_3_0_3_output_4, switch_3_0_3_output_5, switch_3_0_3_output_6,
       switch_3_0_3_output_7, switch_3_0_3_output_8, switch_3_0_3_output_9, switch_3_0_4_output,
       switch_3_0_4_output_2, switch_3_0_4_output_3, switch_3_0_4_output_4, switch_3_0_4_output_5,
       switch_3_0_4_output_6, switch_3_0_4_output_7, switch_3_0_4_output_8, switch_3_0_4_output_9,
       switch_3_0_5_output, switch_3_0_5_output_2, switch_3_0_5_output_3, switch_3_0_5_output_4,
       switch_3_0_5_output_5, switch_3_0_5_output_6, switch_3_0_5_output_7, switch_3_0_5_output_8,
       switch_3_0_5_output_9, switch_3_0_6_output, switch_3_0_6_output_2, switch_3_0_6_output_3,
       switch_3_0_6_output_4, switch_3_0_6_output_5, switch_3_0_6_output_6, switch_3_0_6_output_7,
       switch_3_0_6_output_8, switch_3_0_6_output_9, switch_3_0_7_output, switch_3_0_7_output_2,
       switch_3_0_7_output_3, switch_3_0_7_output_4, switch_3_0_7_output_5, switch_3_0_7_output_6,
       switch_3_0_7_output_7, switch_3_0_7_output_8, switch_3_0_7_output_9, switch_3_0_8_output,
       switch_3_0_8_output_2, switch_3_0_8_output_3, switch_3_0_8_output_4, switch_3_0_8_output_5,
       switch_3_0_8_output_6, switch_3_0_8_output_7, switch_3_0_8_output_8, switch_3_0_8_output_9;

  Clock clock_1 (.out(clock_1_out));
  and and_1 (and_1_out, clock_1_out, bus_0_2);
  Random #(.width(5)) random_1 (.clk(bus_0_2), .out(random_1_out));  // open: next, clr
  Adder adder_1 (.a({{5{1'b0}}, adr}), .b({random_1_out, 3'b000}), .out(adder_1_out));  // open: cin, cout
  // Probe on random_1_out
  Hex_Digit_Display hex_digit_display_1 (.value(counter_invertor_1_output));  // open: dp
  counter_invertor counter_invertor_1 (.\output (counter_invertor_1_output), .\input (life_cntr_1_display));
  DotMatrix #(.matrixcols(9), .matrixrows(9)) dotmatrix_1 (
    .col0(switch_3_0_1_output), .col1(switch_3_0_1_output_2), .col2(switch_3_0_1_output_3),
    .col3(switch_3_0_1_output_4), .col4(switch_3_0_1_output_5), .col5(switch_3_0_1_output_6),
    .col6(switch_3_0_1_output_7), .col7(switch_3_0_1_output_8), .col8(switch_3_0_1_output_9));
  Switch_3_0 switch_3_0_1 (
    .ctrl(r0[7]), .GOLet(5'b00111), .Let(\let ), .Game_over(life_cntr_1_game_over),
    .Output(switch_3_0_1_output), .Output_2(switch_3_0_1_output_2), .Output_3(switch_3_0_1_output_3),
    .Output_4(switch_3_0_1_output_4), .Output_5(switch_3_0_1_output_5), .Output_6(switch_3_0_1_output_6),
    .Output_7(switch_3_0_1_output_7), .Output_8(switch_3_0_1_output_8), .Output_9(switch_3_0_1_output_9),
    .clock(and_2_out));
  Life_cntr life_cntr_1 (
    .Game_over(life_cntr_1_game_over), .flags(r0), .display(life_cntr_1_display), .clock(button_1_out));  // open: reset
  Button button_1 (.out(button_1_out));
  Transistor #(.gate("br")) transistor_1 (.in(and_1_out), .out(transistor_1_out), .gate(counter_1_carry));
  Counter #(.width(3), .max('h7), .ongoal("stay")) counter_1 (
    .Q(adr), .carry(counter_1_carry), .clk(and_1_out));  // open: load, D, count, clr
  Transistor #(.\type ("n"), .width(5)) transistor_2 (.in(5'b00001), .out(bt), .gate(btA));
  Transistor #(.\type ("n"), .width(5)) transistor_3 (.in(5'b01110), .out(bt), .gate(btN));
  Switch_3_0 switch_3_0_2 (
    .ctrl(r0[6]), .GOLet(5'b00001), .Let(\let ), .Game_over(life_cntr_1_game_over),
    .Output(switch_3_0_2_output), .Output_2(switch_3_0_2_output_2), .Output_3(switch_3_0_2_output_3),
    .Output_4(switch_3_0_2_output_4), .Output_5(switch_3_0_2_output_5), .Output_6(switch_3_0_2_output_6),
    .Output_7(switch_3_0_2_output_7), .Output_8(switch_3_0_2_output_8), .Output_9(switch_3_0_2_output_9),
    .clock(and_3_out));
  DotMatrix #(.matrixcols(9), .matrixrows(9)) dotmatrix_2 (
    .col0(switch_3_0_2_output), .col1(switch_3_0_2_output_2), .col2(switch_3_0_2_output_3),
    .col3(switch_3_0_2_output_4), .col4(switch_3_0_2_output_5), .col5(switch_3_0_2_output_6),
    .col6(switch_3_0_2_output_7), .col7(switch_3_0_2_output_8), .col8(switch_3_0_2_output_9));
  and and_2 (and_2_out, transistor_1_out, ~adr[2], ~adr[1], ~adr[0]);  // AND_Gate
  Pull_Resistor pull_resistor_1 (.node(transistor_1_out));
  ROM #(.dataWidth(5)) rom_1 (.addr(adder_1_out), .data(\let ));  // open: sel
  Transistor #(.\type ("n"), .width(5)) transistor_4 (.in(5'b00010), .out(bt), .gate(btB));
  buf buffer_1 (kcl, btA);
  Transistor #(.\type ("n"), .width(5)) transistor_5 (.in(5'b01111), .out(bt), .gate(btO));
  buf buffer_2 (kcl, btN);
  and and_3 (and_3_out, transistor_1_out, ~adr[2], ~adr[1], adr[0]);  // AND_Gate
  Register #(.width(5)) register_1 (.D(bt), .Q(register_1_q), .clk(kcl));  // open: en, clr
  Transistor #(.\type ("n"), .width(5)) transistor_6 (.in(5'b00011), .out(bt), .gate(btC));
  buf buffer_3 (kcl, btC);
  buf buffer_4 (kcl, btB);
  Transistor #(.\type ("n"), .width(5)) transistor_7 (.in(5'b10000), .out(bt), .gate(btP));
  buf buffer_5 (kcl, btO);
  buf buffer_6 (kcl, btP);
  Switch_3_0 switch_3_0_3 (
    .ctrl(r0[5]), .GOLet(5'b01101), .Let(\let ), .Game_over(life_cntr_1_game_over),
    .Output(switch_3_0_3_output), .Output_2(switch_3_0_3_output_2), .Output_3(switch_3_0_3_output_3),
    .Output_4(switch_3_0_3_output_4), .Output_5(switch_3_0_3_output_5), .Output_6(switch_3_0_3_output_6),
    .Output_7(switch_3_0_3_output_7), .Output_8(switch_3_0_3_output_8), .Output_9(switch_3_0_3_output_9),
    .clock(and_4_out));
  DotMatrix #(.matrixcols(9), .matrixrows(9)) dotmatrix_3 (
    .col0(switch_3_0_3_output), .col1(switch_3_0_3_output_2), .col2(switch_3_0_3_output_3),
    .col3(switch_3_0_3_output_4), .col4(switch_3_0_3_output_5), .col5(switch_3_0_3_output_6),
    .col6(switch_3_0_3_output_7), .col7(switch_3_0_3_output_8), .col8(switch_3_0_3_output_9));
  and and_4 (and_4_out, transistor_1_out, ~adr[2], adr[1], ~adr[0]);  // AND_Gate
  assign r0 = bus_0 | cdm_8_mark5_1_p3;  // OR_Gate or_1, 8 bits wide
  Transistor #(.\type ("n")) transistor_8 (.in(cl), .out(transistor_8_out), .gate(counter_1_carry));
  Clock clock_2 (.out(cl));
  Button W (.out(btW));
  Button Q (.out(btQ));
  Button A (.out(btA));
  // Probe on register_1_q
  Pull_Resistor pull_resistor_2 (.node(kcl));
  Button Z (.out(btZ));
  Transistor #(.\type ("n"), .width(5)) transistor_9 (.in(5'b00100), .out(bt), .gate(btD));
  buf buffer_7 (kcl, btD);
  Transistor #(.\type ("n"), .width(5)) transistor_10 (.in(5'b10001), .out(bt), .gate(btQ));
  buf buffer_8 (kcl, btQ);
  Switch_3_0 switch_3_0_4 (
    .ctrl(r0[4]), .GOLet(5'b00101), .Let(\let ), .Game_over(life_cntr_1_game_over),
    .Output(switch_3_0_4_output), .Output_2(switch_3_0_4_output_2), .Output_3(switch_3_0_4_output_3),
    .Output_4(switch_3_0_4_output_4), .Output_5(switch_3_0_4_output_5), .Output_6(switch_3_0_4_output_6),
    .Output_7(switch_3_0_4_output_7), .Output_8(switch_3_0_4_output_8), .Output_9(switch_3_0_4_output_9),
    .clock(and_5_out));
  DotMatrix #(.matrixcols(9), .matrixrows(9)) dotmatrix_4 (
    .col0(switch_3_0_4_output), .col1(switch_3_0_4_output_2), .col2(switch_3_0_4_output_3),
    .col3(switch_3_0_4_output_4), .col4(switch_3_0_4_output_5), .col5(switch_3_0_4_output_6),
    .col6(switch_3_0_4_output_7), .col7(switch_3_0_4_output_8), .col8(switch_3_0_4_output_9));
  // Probe on cdm_8_mark5_1_p4
  // Probe on cdm_8_mark5_1_p7
  // Probe on cdm_8_mark5_1_p8
  // Probe on cdm_8_mark5_1_p6
  // Probe on nothing
  Button Y (.out(btY));
  Button E (.out(btE));
  Button T (.out(btT));
  Button R (.out(btR));
  Button F (.out(btF));
  Button S (.out(btS));
  Button G (.out(btG));
  Button D (.out(btD));
  Button B (.out(btB));
  Button V (.out(btV));
  Button C (.out(btC));
  Button X (.out(btX));
  Transistor #(.\type ("n"), .width(5)) transistor_11 (.in(5'b00101), .out(bt), .gate(btE));
  buf buffer_9 (kcl, btE);
  Transistor #(.\type ("n"), .width(5)) transistor_12 (.in(5'b10010), .out(bt), .gate(btR));
  buf buffer_10 (kcl, btR);
  DotMatrix #(.matrixcols(9), .matrixrows(9)) dotmatrix_5 (
    .col0(switch_3_0_5_output), .col1(switch_3_0_5_output_2), .col2(switch_3_0_5_output_3),
    .col3(switch_3_0_5_output_4), .col4(switch_3_0_5_output_5), .col5(switch_3_0_5_output_6),
    .col6(switch_3_0_5_output_7), .col7(switch_3_0_5_output_8), .col8(switch_3_0_5_output_9));
  Switch_3_0 switch_3_0_5 (
    .ctrl(r0[3]), .GOLet(5'b01111), .Let(\let ), .Game_over(life_cntr_1_game_over),
    .Output(switch_3_0_5_output), .Output_2(switch_3_0_5_output_2), .Output_3(switch_3_0_5_output_3),
    .Output_4(switch_3_0_5_output_4), .Output_5(switch_3_0_5_output_5), .Output_6(switch_3_0_5_output_6),
    .Output_7(switch_3_0_5_output_7), .Output_8(switch_3_0_5_output_8), .Output_9(switch_3_0_5_output_9),
    .clock(and_6_out));
  and and_5 (and_5_out, transistor_1_out, ~adr[2], adr[1], adr[0]);  // AND_Gate
  // Probe on cdm_8_mark5_1_p9
  // CdM_8_mark5 cdm_8_mark5_1: pin names not known; wires that end beside it: halted, btQ, cdm_8_mark5_1_p3, cdm_8_mark5_1_p4, transistor_8_out, cdm_8_mark5_1_p6, cdm_8_mark5_1_p7, cdm_8_mark5_1_p8, cdm_8_mark5_1_p9, cdm_8_mark5_1_p10, cdm_8_mark5_1_p11, rd_wr, cdm_8_mark5_1_p13, cdm_8_mark5_1_p14, cdm_8_mark5_1_p15
  Button U (.out(btU));
  Button I (.out(btI));
  Button P (.out(btP));
  Button O (.out(btO));
  Button K (.out(btK));
  Button J (.out(btJ));
  Button L (.out(btL));
  Button H (.out(btH));
  Button M (.out(btM));
  Button N (.out(btN));
  Transistor #(.\type ("n"), .width(5)) transistor_13 (.in(5'b00110), .out(bt), .gate(btF));
  buf buffer_11 (kcl, btF);
  Transistor #(.\type ("n"), .width(5)) transistor_14 (.in(5'b10011), .out(bt), .gate(btS));
  buf buffer_12 (kcl, btS);
  DotMatrix #(.matrixcols(9), .matrixrows(9)) dotmatrix_6 (
    .col0(switch_3_0_6_output), .col1(switch_3_0_6_output_2), .col2(switch_3_0_6_output_3),
    .col3(switch_3_0_6_output_4), .col4(switch_3_0_6_output_5), .col5(switch_3_0_6_output_6),
    .col6(switch_3_0_6_output_7), .col7(switch_3_0_6_output_8), .col8(switch_3_0_6_output_9));
  Switch_3_0 switch_3_0_6 (
    .ctrl(r0[2]), .GOLet(5'b10110), .Let(\let ), .Game_over(life_cntr_1_game_over),
    .Output(switch_3_0_6_output), .Output_2(switch_3_0_6_output_2), .Output_3(switch_3_0_6_output_3),
    .Output_4(switch_3_0_6_output_4), .Output_5(switch_3_0_6_output_5), .Output_6(switch_3_0_6_output_6),
    .Output_7(switch_3_0_6_output_7), .Output_8(switch_3_0_6_output_8), .Output_9(switch_3_0_6_output_9),
    .clock(and_7_out));
  and and_6 (and_6_out, transistor_1_out, adr[2], ~adr[1], ~adr[0]);  // AND_Gate
  Decoder decoder_1 (.out0(code), .out1(data), .sel(cdm_8_mark5_1_p10), .en(cdm_8_mark5_1_p11));
  assign controlled_buffer_1_out = not_1_out ? cdm_8_mark5_1_p14 : 8'bz;  // Controlled_Buffer controlled_buffer_1
  not not_1 (not_1_out, rd_wr);
  assign cdm_8_mark5_1_p15 = rd_wr ? controlled_buffer_1_out : 8'bz;  // Controlled_Buffer controlled_buffer_2
  Transistor #(.\type ("n"), .width(5)) transistor_15 (.in(5'b00111), .out(bt), .gate(btG));
  buf buffer_13 (kcl, btG);
  Transistor #(.\type ("n"), .width(5)) transistor_16 (.in(5'b10100), .out(bt), .gate(btT));
  buf buffer_14 (kcl, btT);
  and and_7 (and_7_out, transistor_1_out, adr[2], ~adr[1], adr[0]);  // AND_Gate
  Transistor #(.\type ("n"), .width(8)) transistor_17 (
    .in(cdm_8_mark5_1_p13), .out(transistor_17_out), .gate(counter_1_carry));
  Transistor #(.width(8)) transistor_18 (.in({{5{1'b0}}, adr}), .out(transistor_17_out), .gate(counter_1_carry));
  Transistor #(.\type ("n"), .width(5)) transistor_19 (.in(5'b01000), .out(bt), .gate(btH));
  Transistor #(.\type ("n"), .width(5)) transistor_20 (.in(5'b01001), .out(bt), .gate(btI));
  buf buffer_15 (kcl, btH);
  Transistor #(.\type ("n"), .width(5)) transistor_21 (.in(5'b10110), .out(bt), .gate(btV));
  Transistor #(.\type ("n"), .width(5)) transistor_22 (.in(5'b10101), .out(bt), .gate(btU));
  buf buffer_16 (kcl, btU);
  Switch_3_0 switch_3_0_7 (
    .ctrl(r0[1]), .GOLet(5'b00101), .Let(\let ), .Game_over(life_cntr_1_game_over),
    .Output(switch_3_0_7_output), .Output_2(switch_3_0_7_output_2), .Output_3(switch_3_0_7_output_3),
    .Output_4(switch_3_0_7_output_4), .Output_5(switch_3_0_7_output_5), .Output_6(switch_3_0_7_output_6),
    .Output_7(switch_3_0_7_output_7), .Output_8(switch_3_0_7_output_8), .Output_9(switch_3_0_7_output_9),
    .clock(and_8_out));
  DotMatrix #(.matrixcols(9), .matrixrows(9)) dotmatrix_7 (
    .col0(switch_3_0_7_output), .col1(switch_3_0_7_output_2), .col2(switch_3_0_7_output_3),
    .col3(switch_3_0_7_output_4), .col4(switch_3_0_7_output_5), .col5(switch_3_0_7_output_6),
    .col6(switch_3_0_7_output_7), .col7(switch_3_0_7_output_8), .col8(switch_3_0_7_output_9));
  and and_8 (and_8_out, transistor_1_out, adr[2], adr[1], ~adr[0]);  // AND_Gate
  Pull_Resistor pull_resistor_3 (.node(pull_resistor_3_node));
  Transistor #(.\type ("n")) transistor_23 (.in(data), .out(transistor_23_out), .gate(counter_1_carry));
  Transistor #(.\type ("n"), .gate("br")) transistor_24 (
    .in(rd_wr), .out(pull_resistor_3_node), .gate(counter_1_carry));
  Transistor #(.\type ("n"), .width(5)) transistor_25 (.in(5'b01010), .out(bt), .gate(btJ));
  buf buffer_17 (kcl, btI);
  Transistor #(.\type ("n"), .width(5)) transistor_26 (.in(5'b10111), .out(bt), .gate(btW));
  buf buffer_18 (kcl, btV);
  Switch_3_0 switch_3_0_8 (
    .ctrl(r0[0]), .GOLet(5'b10010), .Let(\let ), .Game_over(life_cntr_1_game_over),
    .Output(switch_3_0_8_output), .Output_2(switch_3_0_8_output_2), .Output_3(switch_3_0_8_output_3),
    .Output_4(switch_3_0_8_output_4), .Output_5(switch_3_0_8_output_5), .Output_6(switch_3_0_8_output_6),
    .Output_7(switch_3_0_8_output_7), .Output_8(switch_3_0_8_output_8), .Output_9(switch_3_0_8_output_9),
    .clock(and_9_out));
  DotMatrix #(.matrixcols(9), .matrixrows(9)) dotmatrix_8 (
    .col0(switch_3_0_8_output), .col1(switch_3_0_8_output_2), .col2(switch_3_0_8_output_3),
    .col3(switch_3_0_8_output_4), .col4(switch_3_0_8_output_5), .col5(switch_3_0_8_output_6),
    .col6(switch_3_0_8_output_7), .col7(switch_3_0_8_output_8), .col8(switch_3_0_8_output_9));
  ROM rom_2 (.addr(cdm_8_mark5_1_p13), .data(rom_2_data), .sel(code));
  Transistor #(.\type ("n"), .gate("br"), .width(8)) transistor_27 (
    .in(rom_2_data), .out(controlled_buffer_1_out), .gate(counter_1_carry));
  Transistor #(.width(8)) transistor_28 (.in({3'b000, \let }), .out(controlled_buffer_1_out), .gate(counter_1_carry));
  RAM ram_1 (
    .addr(transistor_17_out), .data(controlled_buffer_1_out), .sel(transistor_23_out), .clk(cl),
    .ld(pull_resistor_3_node));  // open: clr
  Transistor #(.\type ("n"), .width(5)) transistor_29 (.in(5'b01011), .out(bt), .gate(btK));
  buf buffer_19 (kcl, btJ);
  buf buffer_20 (kcl, btK);
  Transistor #(.\type ("n"), .width(5)) transistor_30 (.in(5'b11000), .out(bt), .gate(btX));
  buf buffer_21 (kcl, btW);
  buf buffer_22 (kcl, btX);
  and and_9 (and_9_out, transistor_1_out, adr[2], adr[1], adr[0]);
  Transistor #(.\type ("n"), .width(5)) transistor_31 (.in(5'b01100), .out(bt), .gate(btL));
  buf buffer_23 (kcl, btL);
  Transistor #(.\type ("n"), .width(5)) transistor_32 (.in(5'b11001), .out(bt), .gate(btY));
  buf buffer_24 (kcl, btY);
  RAM ram_2 (
    .addr({{5{1'b0}}, adr}), .data({ram_2_data, \let }), .clk(cl), .ld(pull_resistor_4_node));  // open: sel, clr
  Pull_Resistor pull_resistor_4 (.node(pull_resistor_4_node));
  Transistor #(.\type ("n"), .width(5)) transistor_33 (.in(5'b01101), .out(bt), .gate(btM));
  buf buffer_25 (kcl, btM);
  Transistor #(.\type ("n"), .width(5)) transistor_34 (.in(5'b11010), .out(bt), .gate(btZ));
  buf buffer_26 (kcl, btZ);
  // also tied to GND on the sheet: {ram_2_data[5], ram_2_data[6], ram_2_data[7]}

  // Notes on the sheet:
  //   LIVES
  //   contents of rom_1 (hex, n*v repeats v):
  //   1 2 13 f c 15 14 5 3 1 c 5 e 4 1 12 5 c 5 10 8 1 e 14 d f 15 e 14 1 9 e 10 1 12 1 4 9 13 5 15 c 14 9
  //   d 1 14 5 17 1 14 5 12 6 1 c 18 5 e f 10 8 f 2 3 f d 10 15 14 5 12 5 e 7 9 e 5 5 12 6 5 13 14 9 16 1
  //   c 4 9 13 3 f 16 5 12 e 1 16 9 7 1 14 5 f 10 5 12 1 14 f 12 7 5 e 5 12 1 14 5 2 5 1 15 14 9 6 19 2 15
  //   9 c 4 9 e 7 3 8 9 c 4 12 5 e 8 f 13 10 9 14 1 c b 9 14 3 8 5 e 13 c 1 e 7 15 1 7 5 d 9 13 14 1 b 5
  //   13 e f 14 5 2 f f b 10 1 e 14 9 e 7 7 11 15 5 13 14 9 f e 12 5 13 5 1 12 3 8 13 f 6 14 17 1 12 5 13
  //   14 12 1 14 5 7 19 14 12 1 9 e 9 e 7 16 1 3 1 14 9 f e
  //   buffer_1 drives only 1 and floats otherwise
  //   buffer_2 drives only 1 and floats otherwise
  //   reset
  //   buffer_3 drives only 1 and floats otherwise
  //   buffer_4 drives only 1 and floats otherwise
  //   buffer_5 drives only 1 and floats otherwise
  //   buffer_6 drives only 1 and floats otherwise
  //   buffer_7 drives only 1 and floats otherwise
  //   buffer_8 drives only 1 and floats otherwise
  //   buffer_9 drives only 1 and floats otherwise
  //   buffer_10 drives only 1 and floats otherwise
  //   buffer_11 drives only 1 and floats otherwise
  //   buffer_12 drives only 1 and floats otherwise
  //   buffer_13 drives only 1 and floats otherwise
  //   buffer_14 drives only 1 and floats otherwise
  //   buffer_15 drives only 1 and floats otherwise
  //   buffer_16 drives only 1 and floats otherwise
  //   buffer_17 drives only 1 and floats otherwise
  //   buffer_18 drives only 1 and floats otherwise
  //   contents of rom_2 (hex, n*v repeats v):
  //   d0 0 d1 80 d2 0 c2 ba a e0 17 d3 18 ff 7b e1 12 54 c6 8e 91 ee 6 d4 1
  //   buffer_19 drives only 1 and floats otherwise
  //   buffer_20 drives only 1 and floats otherwise
  //   buffer_21 drives only 1 and floats otherwise
  //   buffer_22 drives only 1 and floats otherwise
  //   buffer_23 drives only 1 and floats otherwise
  //   buffer_24 drives only 1 and floats otherwise
  //   buffer_25 drives only 1 and floats otherwise
  //   buffer_26 drives only 1 and floats otherwise
endmodule

module Alphabet (
);

  DotMatrix #(.matrixcols(9), .matrixrows(9)) dotmatrix_1 (
    .col0({9{1'b0}}), .col1(9'h2), .col2(9'h7e), .col3(9'h90), .col4(9'h92), .col5(9'hfe), .col6(9'h7e),
    .col7(9'h2), .col8({9{1'b0}}));
  DotMatrix #(.matrixcols(9), .matrixrows(9)) dotmatrix_2 (
    .col0({9{1'b0}}), .col1(9'h8), .col2(9'he), .col3(9'hc2), .col4(9'h82), .col5(9'hfe), .col6(9'hfc),
    .col7(9'h80), .col8({9{1'b0}}));
  DotMatrix #(.matrixcols(9), .matrixrows(9)) dotmatrix_3 (
    .col0({9{1'b0}}), .col1(9'h64), .col2(9'hf4), .col3(9'h92), .col4(9'h92), .col5(9'h92), .col6(9'hde),
    .col7(9'h4c), .col8({9{1'b0}}));
  DotMatrix #(.matrixcols(9), .matrixrows(9)) dotmatrix_4 (
    .col0({9{1'b0}}), .col1(9'h82), .col2(9'hfe), .col3(9'hfe), .col4(9'h92), .col5(9'h92), .col6(9'hfe),
    .col7(9'h6c), .col8({9{1'b0}}));
  DotMatrix #(.matrixcols(9), .matrixrows(9)) dotmatrix_5 (
    .col0({9{1'b0}}), .col1(9'h82), .col2(9'hfe), .col3(9'hfe), .col4(9'h92), .col5(9'h30), .col6(9'hde),
    .col7(9'h82), .col8({9{1'b0}}));
  DotMatrix #(.matrixcols(9), .matrixrows(9)) dotmatrix_6 (
    .col0({9{1'b0}}), .col1(9'hc0), .col2(9'h82), .col3(9'hfe), .col4(9'hfe), .col5(9'h82), .col6(9'hc0),
    .col7(9'hc0), .col8({9{1'b0}}));
  DotMatrix #(.matrixcols(9), .matrixrows(9)) dotmatrix_7 (
    .col0({9{1'b0}}), .col1(9'h7c), .col2(9'hfe), .col3(9'h82), .col4(9'h82), .col5(9'h82), .col6(9'hc6),
    .col7(9'h64), .col8({9{1'b0}}));
  DotMatrix #(.matrixcols(9), .matrixrows(9)) dotmatrix_8 (
    .col0({9{1'b0}}), .col1(9'h82), .col2(9'hfe), .col3(9'hfe), .col4(9'h2), .col5(9'h2), .col6(9'h2),
    .col7(9'he), .col8({9{1'b0}}));
  DotMatrix #(.matrixcols(9), .matrixrows(9)) dotmatrix_9 (
    .col0({9{1'b0}}), .col1(9'h80), .col2(9'hfc), .col3(9'h6), .col4(9'h86), .col5(9'hfe), .col6(9'hfc),
    .col7(9'h80), .col8({9{1'b0}}));
  DotMatrix #(.matrixcols(9), .matrixrows(9)) dotmatrix_10 (
    .col0({9{1'b0}}), .col1(9'h82), .col2(9'hfe), .col3(9'hfe), .col4(9'h82), .col5(9'h82), .col6(9'hfe),
    .col7(9'h7c), .col8({9{1'b0}}));
  DotMatrix #(.matrixcols(9), .matrixrows(9)) dotmatrix_11 (
    .col0({9{1'b0}}), .col1(9'hfe), .col2(9'hfe), .col3(9'h22), .col4(9'h10), .col5(9'h60), .col6(9'hfe),
    .col7(9'hfe), .col8({9{1'b0}}));
  DotMatrix #(.matrixcols(9), .matrixrows(9)) dotmatrix_12 (
    .col0({9{1'b0}}), .col1(9'he0), .col2(9'h18), .col3(9'h6), .col4(9'h9e), .col5(9'hf8), .col6(9'he0),
    .col7(9'h80), .col8({9{1'b0}}));
  DotMatrix #(.matrixcols(9), .matrixrows(9)) dotmatrix_13 (
    .col0({9{1'b0}}), .col1(9'h82), .col2(9'hfe), .col3(9'hfe), .col4(9'h92), .col5(9'h92), .col6(9'h82),
    .col7(9'hc6), .col8({9{1'b0}}));
  DotMatrix #(.matrixcols(9), .matrixrows(9)) dotmatrix_14 (
    .col0({9{1'b0}}), .col1(9'hfe), .col2(9'hfe), .col3(9'h60), .col4(9'h10), .col5(9'hc), .col6(9'hfe),
    .col7(9'hfe), .col8({9{1'b0}}));
  DotMatrix #(.matrixcols(9), .matrixrows(9)) dotmatrix_15 (
    .col0({9{1'b0}}), .col1(9'hf8), .col2(9'he), .col3(9'h30), .col4(9'h78), .col5(9'hc), .col6(9'hfe),
    .col7(9'hf8), .col8({9{1'b0}}));
  DotMatrix #(.matrixcols(9), .matrixrows(9)) dotmatrix_16 (
    .col0({9{1'b0}}), .col1(9'h82), .col2(9'hfe), .col3(9'hfe), .col4(9'h92), .col5(9'h90), .col6(9'h80),
    .col7(9'hc0), .col8({9{1'b0}}));
  DotMatrix #(.matrixcols(9), .matrixrows(9)) dotmatrix_17 (
    .col0({9{1'b0}}), .col1(9'h7c), .col2(9'hfe), .col3(9'h82), .col4(9'h82), .col5(9'h82), .col6(9'hfe),
    .col7(9'h7c), .col8({9{1'b0}}));
  DotMatrix #(.matrixcols(9), .matrixrows(9)) dotmatrix_18 (
    .col0({9{1'b0}}), .col1(9'h82), .col2(9'hc6), .col3(9'h28), .col4(9'h10), .col5(9'hee), .col6(9'hc6),
    .col7(9'h82), .col8({9{1'b0}}));
  DotMatrix #(.matrixcols(9), .matrixrows(9)) dotmatrix_19 (
    .col0({9{1'b0}}), .col1(9'h7c), .col2(9'hfe), .col3(9'h82), .col4(9'h92), .col5(9'h9e), .col6(9'hde),
    .col7(9'h50), .col8({9{1'b0}}));
  DotMatrix #(.matrixcols(9), .matrixrows(9)) dotmatrix_20 (
    .col0({9{1'b0}}), .col1(9'h82), .col2(9'hfe), .col3(9'hfe), .col4(9'h8a), .col5(9'h88), .col6(9'hf8),
    .col7(9'h70), .col8({9{1'b0}}));
  DotMatrix #(.matrixcols(9), .matrixrows(9)) dotmatrix_21 (
    .col0({9{1'b0}}), .col1(9'h80), .col2(9'he0), .col3(9'h22), .col4(9'h9e), .col5(9'hfe), .col6(9'he2),
    .col7(9'h80), .col8({9{1'b0}}));
  DotMatrix #(.matrixcols(9), .matrixrows(9)) dotmatrix_22 (
    .col0({9{1'b0}}), .col1(9'h82), .col2(9'hfe), .col3(9'h92), .col4(9'h10), .col5(9'hfe), .col6(9'hfe),
    .col7(9'h82), .col8({9{1'b0}}));
  DotMatrix #(.matrixcols(9), .matrixrows(9)) dotmatrix_23 (
    .col0({9{1'b0}}), .col1(9'h7c), .col2(9'hfe), .col3(9'h82), .col4(9'h88), .col5(9'h86), .col6(9'hfe),
    .col7(9'h7a), .col8({9{1'b0}}));
  DotMatrix #(.matrixcols(9), .matrixrows(9)) dotmatrix_24 (
    .col0({9{1'b0}}), .col1(9'he2), .col2(9'h86), .col3(9'h8e), .col4(9'h92), .col5(9'he2), .col6(9'hc2),
    .col7(9'h8e), .col8({9{1'b0}}));
  DotMatrix #(.matrixcols(9), .matrixrows(9)) dotmatrix_25 (
    .col0({9{1'b0}}), .col1(9'hc6), .col2(9'h82), .col3(9'hfe), .col4(9'hfe), .col5(9'h82), .col6(9'hc6),
    .col7(9'hc6), .col8({9{1'b0}}));
  DotMatrix #(.matrixcols(9), .matrixrows(9)) dotmatrix_26 (
    .col0({9{1'b0}}), .col1(9'hfe), .col2(9'hfe), .col3(9'h92), .col4(9'h98), .col5(9'h98), .col6(9'hf6),
    .col7(9'h62), .col8({9{1'b0}}));
  DotMatrix #(.matrixcols(9), .matrixrows(9)) dotmatrix_27 (
    .col0({9{1'b0}}), .col1(9'h7f), .col2(9'h80), .col3(9'h108), .col4(9'h100), .col5(9'h100), .col6(9'h80),
    .col7(9'h7f), .col8({9{1'b0}}));
endmodule

module answers (
);


  // Notes on the sheet:
  //   50) FESTIVAL; DISCOVER
  //   70) GENERATE; BEAUTIFY
  //   80) BUILDING; CHILDREN
  //   90) HOSPITAL; KITCHEN
  //   a0) LANGUAGE; MISTAKES
  //   b0) NOTEBOOK; PAINTING
  //   c0) QUESTION; RECEARCH
  //   d0)SOFTWARE; STRATEGY
  //   e0)TRAINING; VACATION
  //   00) ABSOLUTE; CALENDAR
  //   10) ELEPHANT; MOUNTAIN
  //   20) PARADISE; ULTIMATE 
  //   30) WATERFAL; XENOPHOB
  //   40) COMPUTER; ENGINEER
  //   60) NAVIGATE; OPERATOR
endmodule

module Switch_3_0 (
  input  ctrl,
  input  [4:0] GOLet,
  input  [4:0] Let,
  input  Game_over,
  input  clock,
  output [8:0] Output,
  output [8:0] Output_2,
  output [8:0] Output_3,
  output [8:0] Output_4,
  output [8:0] Output_5,
  output [8:0] Output_6,
  output [8:0] Output_7,
  output [8:0] Output_8,
  output [8:0] Output_9
);

  wire transistor_2_out, transistor_7_out;
  wire [4:0] let_t, transistor_5_out;
  wire [8:0] multiplexer_1_out, multiplexer_1_out_2, multiplexer_1_out_3, multiplexer_2_out,
       multiplexer_2_out_2, multiplexer_2_out_3, multiplexer_3_out, multiplexer_3_out_2, multiplexer_3_out_3;

  Transistor #(.\type ("n"), .width(9)) transistor_1 (.in(multiplexer_1_out_3), .out(Output), .gate(transistor_2_out));
  Transistor #(.gate("br")) transistor_2 (.in(ctrl), .out(transistor_2_out), .gate(Game_over));
  Transistor #(.\type ("n"), .gate("br")) transistor_3 (.in(1'b1), .out(transistor_2_out), .gate(Game_over));
  Transistor #(.\type ("n"), .width(9)) transistor_4 (
    .in(multiplexer_1_out_2), .out(Output_2), .gate(transistor_2_out));
  Multiplexer #(.select(5), .width(27), .enable("false")) multiplexer_1 (
    .in0({27{1'b0}}), .in1(27'h47e), .in2(27'h104fe), .in3(27'hf8fe), .in4(27'h104fe), .in5(27'h104fe),
    .in6(27'h104fe), .in7(27'hf8fe), .in8(27'h104fe), .in9(27'h18c82), .in10(27'h100e), .in11(27'h104fe),
    .in12(27'h104fe), .in13(27'h1fcfe), .in14(27'h1fcfe), .in15(27'hf8fe), .in16(27'h104fe), .in17(27'hf8fe),
    .in18(27'h1fcfe), .in19(27'hc8f4), .in20(27'h18082), .in21(27'h100fc), .in22(27'h1c018),
    .in23(27'h1f00e), .in24(27'h104c6), .in25(27'h100e0), .in26(27'h1c486), .in27({27{1'b0}}),
    .in28({27{1'b0}}), .in29({27{1'b0}}), .in30({27{1'b0}}), .in31({27{1'b0}}),
    .out({multiplexer_1_out_3, multiplexer_1_out_2, multiplexer_1_out}), .sel(let_t));
  Transistor #(.\type ("n"), .gate("br"), .width(5)) transistor_5 (
    .in(GOLet), .out(transistor_5_out), .gate(Game_over));
  Transistor #(.gate("br"), .width(5)) transistor_6 (.in(Let), .out(transistor_5_out), .gate(Game_over));
  Transistor #(.\type ("n")) transistor_7 (.in(1'b1), .out(transistor_7_out), .gate(Game_over));
  Transistor transistor_8 (.in(clock), .out(transistor_7_out), .gate(Game_over));
  Transistor #(.\type ("n"), .width(9)) transistor_9 (.in(multiplexer_1_out), .out(Output_3), .gate(transistor_2_out));
  Register #(.width(5)) register_1 (.D(transistor_5_out), .Q(let_t), .clk(transistor_7_out));  // open: en, clr
  Transistor #(.\type ("n"), .width(9)) transistor_10 (
    .in(multiplexer_2_out_3), .out(Output_4), .gate(transistor_2_out));
  Transistor #(.\type ("n"), .width(9)) transistor_11 (
    .in(multiplexer_2_out_2), .out(Output_5), .gate(transistor_2_out));
  Multiplexer #(.select(5), .width(27), .enable("false")) multiplexer_2 (
    .in0({27{1'b0}}), .in1(27'h24124fe), .in2(27'h3f92492), .in3(27'h2090482), .in4(27'h3f90482),
    .in5(27'h3f92492), .in6(27'h3f92490), .in7(27'h209249e), .in8(27'h24820fe), .in9(27'h3f9fc82),
    .in10(27'h30904fe), .in11(27'h3f92430), .in12(27'h3f80402), .in13(27'h882060), .in14(27'h180200c),
    .in15(27'h2090482), .in16(27'h3f91488), .in17(27'h2091086), .in18(27'h2493098), .in19(27'h2492492),
    .in20(27'h3f9fc82), .in21(27'h190cfe), .in22(27'h193cf8), .in23(27'hc0f00c), .in24(27'ha020ee),
    .in25(27'h893cfe), .in26(27'h23924e2), .in27({27{1'b0}}), .in28({27{1'b0}}), .in29({27{1'b0}}),
    .in30({27{1'b0}}), .in31({27{1'b0}}),
    .out({multiplexer_2_out_3, multiplexer_2_out_2, multiplexer_2_out}), .sel(let_t));
  Transistor #(.\type ("n"), .width(9)) transistor_12 (.in(multiplexer_2_out), .out(Output_6), .gate(transistor_2_out));
  Transistor #(.\type ("n"), .width(9)) transistor_13 (
    .in(multiplexer_3_out_3), .out(Output_7), .gate(transistor_2_out));
  Transistor #(.\type ("n"), .width(9)) transistor_14 (
    .in(multiplexer_3_out_2), .out(Output_8), .gate(transistor_2_out));
  Multiplexer #(.select(5), .width(27), .enable("false")) multiplexer_3 (
    .in0({27{1'b0}}), .in1(27'h1f80400), .in2(27'h3f8d800), .in3(27'h318c800), .in4(27'h3f8f800),
    .in5(27'h2098c00), .in6(27'h2018000), .in7(27'h378a000), .in8(27'h3f90400), .in9(27'h3198c00),
    .in10(27'h3f10000), .in11(27'h3790400), .in12(27'h81c00), .in13(27'h3f9fc00), .in14(27'h3f9fc00),
    .in15(27'h3f8f800), .in16(27'h3e0e000), .in17(27'h3f8f400), .in18(27'h3d8c400), .in19(27'h3789800),
    .in20(27'h3018000), .in21(27'h3f10000), .in22(27'h3810000), .in23(27'h3f9f000), .in24(27'h3190400),
    .in25(27'h3890000), .in26(27'h3091c00), .in27({27{1'b0}}), .in28({27{1'b0}}), .in29({27{1'b0}}),
    .in30({27{1'b0}}), .in31({27{1'b0}}),
    .out({multiplexer_3_out_3, multiplexer_3_out_2, multiplexer_3_out}), .sel(let_t));
  Transistor #(.\type ("n"), .width(9)) transistor_15 (.in(multiplexer_3_out), .out(Output_9), .gate(transistor_2_out));
  Transistor #(.gate("br"), .width(9)) transistor_16 (.in({9{1'b0}}), .out(Output), .gate(transistor_2_out));
  Transistor #(.gate("br"), .width(9)) transistor_17 (.in(9'h7f), .out(Output_2), .gate(transistor_2_out));
  Transistor #(.gate("br"), .width(9)) transistor_18 (.in(9'h80), .out(Output_3), .gate(transistor_2_out));
  Transistor #(.gate("br"), .width(9)) transistor_19 (.in(9'h108), .out(Output_4), .gate(transistor_2_out));
  Transistor #(.gate("br"), .width(9)) transistor_20 (.in(9'h100), .out(Output_5), .gate(transistor_2_out));
  Transistor #(.gate("br"), .width(9)) transistor_21 (.in(9'h100), .out(Output_6), .gate(transistor_2_out));
  Transistor #(.gate("br"), .width(9)) transistor_22 (.in(9'h80), .out(Output_7), .gate(transistor_2_out));
  Transistor #(.gate("br"), .width(9)) transistor_23 (.in(9'h7f), .out(Output_8), .gate(transistor_2_out));
  Transistor #(.gate("br"), .width(9)) transistor_24 (.in({9{1'b0}}), .out(Output_9), .gate(transistor_2_out));

  // Other names for the same wires on the sheet: GO = Game_over
endmodule

module Life_cntr (
  input  [7:0] flags,
  input  clock,
  input  reset,
  output [3:0] display,
  output Game_over
);

  wire comparator_1_eq;
  wire [7:0] register_1_q;

  Register register_1 (.D(flags), .Q(register_1_q), .clk(clock), .clr(reset));  // open: en
  Comparator comparator_1 (.a(flags), .b(register_1_q), .eq(comparator_1_eq));  // open: gt, lt
  Counter #(.width(2), .max('h3), .ongoal("stay")) counter_1 (
    .count(comparator_1_eq), .Q(display[1:0]), .carry(Game_over), .clk(clock), .clr(reset));  // open: load, D

  assign display[3:2] = 2'b00;
endmodule

module counter_invertor (
  input  [3:0] \input ,
  output [3:0] \output 
);

  not not_1 (\output [1], \input [1]);
  not not_2 (\output [0], \input [0]);

  assign \output [3:2] = \input [3:2];
endmodule
