// Logisim project CSProject 5.7.circ as structural Verilog: 11 circuits, main circuit main
module main (
);

  wire and_1_out, and_2_out, btA, btB, btC, btD, btE, btF, btG, btH, btI, btJ, btK, btL, btM, btN, btO, btP,
       btQ, btR, btS, btT, btU, btV, btW, btX, btY, btZ, cdm_8_mark5_1_data_inst, cdm_8_mark5_1_mem_cycle,
       cl, clock_1_out, code, data, enter, GO, halt, kcl, ld, ldf, n0_1_out, n1_1_out, n2_1_out, n3_1_out,
       n4_1_out, n5_1_out, n6_1_out, n7_1_out, not_1_out, or_1_out, or_2_out, rd_wr, reset,
       transistor_13_out, WIN;
  wire [3:0] adr, counter_invertor_1_output, life_cntr_1_display;
  wire [4:0] bt, \let , random_1_out, wrd;
  wire [7:0] adder_1_out, cdm_8_mark5_1_addr, cdm_8_mark5_1_data_out, cdm_8_mark5_1_pc, cdm_8_mark5_1_ps,
       cdm_8_mark5_1_r1, cdm_8_mark5_1_r2, cdm_8_mark5_1_r3, cdm_8_mark5_1_sp, controlled_buffer_1_out,
       controlled_buffer_2_out, r0, ram_adress_controller_1_out, rom_2_data;
  wire [7:4] counter_1_out;
  wire [8:0] basic_switch_1_output, basic_switch_1_output_2, basic_switch_1_output_3,
       basic_switch_1_output_4, basic_switch_1_output_5, basic_switch_1_output_6, basic_switch_1_output_7,
       basic_switch_1_output_8, basic_switch_1_output_9, switch_3_0_1_output, switch_3_0_1_output_2,
       switch_3_0_1_output_3, switch_3_0_1_output_4, switch_3_0_1_output_5, switch_3_0_1_output_6,
       switch_3_0_1_output_7, switch_3_0_1_output_8, switch_3_0_1_output_9, switch_3_0_2_output,
       switch_3_0_2_output_2, switch_3_0_2_output_3, switch_3_0_2_output_4, switch_3_0_2_output_5,
       switch_3_0_2_output_6, switch_3_0_2_output_7, switch_3_0_2_output_8, switch_3_0_2_output_9,
       switch_3_0_3_output, switch_3_0_3_output_2, switch_3_0_3_output_3, switch_3_0_3_output_4,
       switch_3_0_3_output_5, switch_3_0_3_output_6, switch_3_0_3_output_7, switch_3_0_3_output_8,
       switch_3_0_3_output_9, switch_3_0_4_output, switch_3_0_4_output_2, switch_3_0_4_output_3,
       switch_3_0_4_output_4, switch_3_0_4_output_5, switch_3_0_4_output_6, switch_3_0_4_output_7,
       switch_3_0_4_output_8, switch_3_0_4_output_9, switch_3_0_5_output, switch_3_0_5_output_2,
       switch_3_0_5_output_3, switch_3_0_5_output_4, switch_3_0_5_output_5, switch_3_0_5_output_6,
       switch_3_0_5_output_7, switch_3_0_5_output_8, switch_3_0_5_output_9, switch_3_0_6_output,
       switch_3_0_6_output_2, switch_3_0_6_output_3, switch_3_0_6_output_4, switch_3_0_6_output_5,
       switch_3_0_6_output_6, switch_3_0_6_output_7, switch_3_0_6_output_8, switch_3_0_6_output_9,
       switch_3_0_7_output, switch_3_0_7_output_2, switch_3_0_7_output_3, switch_3_0_7_output_4,
       switch_3_0_7_output_5, switch_3_0_7_output_6, switch_3_0_7_output_7, switch_3_0_7_output_8,
       switch_3_0_7_output_9, switch_3_0_8_output, switch_3_0_8_output_2, switch_3_0_8_output_3,
       switch_3_0_8_output_4, switch_3_0_8_output_5, switch_3_0_8_output_6, switch_3_0_8_output_7,
       switch_3_0_8_output_8, switch_3_0_8_output_9;

  Clock clock_1 (.out(clock_1_out));
  counter_invertor counter_invertor_1 (.\output (counter_invertor_1_output), .\input (life_cntr_1_display));
  Hex_Digit_Display hex_digit_display_1 (.value(counter_invertor_1_output));  // open: dp
  DotMatrix #(.matrixcols(9), .matrixrows(9)) dotmatrix_1 (
    .col0(switch_3_0_1_output), .col1(switch_3_0_1_output_2), .col2(switch_3_0_1_output_3),
    .col3(switch_3_0_1_output_4), .col4(switch_3_0_1_output_5), .col5(switch_3_0_1_output_6),
    .col6(switch_3_0_1_output_7), .col7(switch_3_0_1_output_8), .col8(switch_3_0_1_output_9));
  Switch_3_0 switch_3_0_1 (
    .ctrl(r0[7]), .GOLet(5'b00111), .Let(wrd), .Output(switch_3_0_1_output),
    .Output_2(switch_3_0_1_output_2), .Output_3(switch_3_0_1_output_3), .Output_4(switch_3_0_1_output_4),
    .Output_5(switch_3_0_1_output_5), .Output_6(switch_3_0_1_output_6), .Output_7(switch_3_0_1_output_7),
    .Output_8(switch_3_0_1_output_8), .Output_9(switch_3_0_1_output_9), .clock(n7_1_out), .reset(reset),
    .Win(WIN), .WINLet(5'b11001), .Game_over(GO));
  Life_cntr life_cntr_1 (
    .Game_over(GO), .flags(r0), .display(life_cntr_1_display), .clock(halt), .reset(reset), .start(halt));
  Comparator comparator_1 (.a(r0), .b({8{1'b1}}), .eq(WIN));  // open: gt, lt
  or or_1 (or_1_out, WIN, GO);
  Transistor transistor_1 (.in(clock_1_out), .out(cl), .gate(or_1_out));
  // Probe on random_1_out
  Random #(.width(5)) random_1 (.clk(1'b1), .out(random_1_out), .clr(reset));  // open: next
  Register #(.width(5)) register_1 (.D(bt), .Q(\let ), .clk(kcl), .clr(reset));  // open: en
  // Probe on \let 
  Pull_Resistor pull_resistor_1 (.node(kcl));
  DotMatrix #(.matrixcols(9), .matrixrows(9)) dotmatrix_2 (
    .col0(switch_3_0_2_output), .col1(switch_3_0_2_output_2), .col2(switch_3_0_2_output_3),
    .col3(switch_3_0_2_output_4), .col4(switch_3_0_2_output_5), .col5(switch_3_0_2_output_6),
    .col6(switch_3_0_2_output_7), .col7(switch_3_0_2_output_8), .col8(switch_3_0_2_output_9));
  Switch_3_0 switch_3_0_2 (
    .ctrl(r0[6]), .GOLet(5'b00001), .Let(wrd), .Output(switch_3_0_2_output),
    .Output_2(switch_3_0_2_output_2), .Output_3(switch_3_0_2_output_3), .Output_4(switch_3_0_2_output_4),
    .Output_5(switch_3_0_2_output_5), .Output_6(switch_3_0_2_output_6), .Output_7(switch_3_0_2_output_7),
    .Output_8(switch_3_0_2_output_8), .Output_9(switch_3_0_2_output_9), .clock(n6_1_out), .reset(reset),
    .Win(WIN), .WINLet(5'b01111), .Game_over(GO));
  _7 u_7_1 (.out(n7_1_out), .clock(ld), .adr(adr));
  Pull_Resistor pull_resistor_2 (.node(ld));
  Transistor #(.gate("br")) transistor_2 (.in(cl), .out(ld), .gate(ldf));
  Adder adder_1 (.a({4'b0000, adr}), .b({random_1_out, 3'b000}), .out(adder_1_out));  // open: cin, cout
  Transistor #(.\type ("n"), .width(5)) transistor_3 (.in(5'b00001), .out(bt), .gate(btA));
  Transistor #(.\type ("n"), .width(5)) transistor_4 (.in(5'b01110), .out(bt), .gate(btN));
  _6 u_6_1 (.out(n6_1_out), .clock(ld), .adr(adr));
  Button New_Game (.out(reset));
  Counter counter_1 (.Max(8'h7), .out({counter_1_out, adr}), .\end (ldf), .clock(cl), .reset(reset));
  Transistor #(.\type ("n"), .width(5)) transistor_5 (.in(5'b00010), .out(bt), .gate(btB));
  buf buffer_1 (kcl, btB);
  buf buffer_2 (kcl, btA);
  Transistor #(.\type ("n"), .width(5)) transistor_6 (.in(5'b01111), .out(bt), .gate(btO));
  buf buffer_3 (kcl, btN);
  buf buffer_4 (kcl, btO);
  Switch_3_0 switch_3_0_3 (
    .ctrl(r0[5]), .GOLet(5'b01101), .Let(wrd), .Output(switch_3_0_3_output),
    .Output_2(switch_3_0_3_output_2), .Output_3(switch_3_0_3_output_3), .Output_4(switch_3_0_3_output_4),
    .Output_5(switch_3_0_3_output_5), .Output_6(switch_3_0_3_output_6), .Output_7(switch_3_0_3_output_7),
    .Output_8(switch_3_0_3_output_8), .Output_9(switch_3_0_3_output_9), .clock(n5_1_out), .reset(reset),
    .Win(WIN), .WINLet(5'b10101), .Game_over(GO));
  DotMatrix #(.matrixcols(9), .matrixrows(9)) dotmatrix_3 (
    .col0(switch_3_0_3_output), .col1(switch_3_0_3_output_2), .col2(switch_3_0_3_output_3),
    .col3(switch_3_0_3_output_4), .col4(switch_3_0_3_output_5), .col5(switch_3_0_3_output_6),
    .col6(switch_3_0_3_output_7), .col7(switch_3_0_3_output_8), .col8(switch_3_0_3_output_9));
  _5 u_5_1 (.out(n5_1_out), .clock(ld), .adr(adr));
  Button W (.out(btW));
  Button Q (.out(btQ));
  Button E (.out(btE));
  Button D (.out(btD));
  Button S (.out(btS));
  Button A (.out(btA));
  Button Z (.out(btZ));
  Button X (.out(btX));
  ROM #(.dataWidth(5)) rom_1 (.addr(adder_1_out), .data(wrd));  // open: sel
  Transistor #(.\type ("n"), .width(5)) transistor_7 (.in(5'b00011), .out(bt), .gate(btC));
  buf buffer_5 (kcl, btC);
  Transistor #(.\type ("n"), .width(5)) transistor_8 (.in(5'b10000), .out(bt), .gate(btP));
  buf buffer_6 (kcl, btP);
  Switch_3_0 switch_3_0_4 (
    .ctrl(r0[4]), .GOLet(5'b00101), .Let(wrd), .Output(switch_3_0_4_output),
    .Output_2(switch_3_0_4_output_2), .Output_3(switch_3_0_4_output_3), .Output_4(switch_3_0_4_output_4),
    .Output_5(switch_3_0_4_output_5), .Output_6(switch_3_0_4_output_6), .Output_7(switch_3_0_4_output_7),
    .Output_8(switch_3_0_4_output_8), .Output_9(switch_3_0_4_output_9), .clock(n4_1_out), .reset(reset),
    .Win(WIN), .WINLet({5{1'b0}}), .Game_over(GO));
  DotMatrix #(.matrixcols(9), .matrixrows(9)) dotmatrix_4 (
    .col0(switch_3_0_4_output), .col1(switch_3_0_4_output_2), .col2(switch_3_0_4_output_3),
    .col3(switch_3_0_4_output_4), .col4(switch_3_0_4_output_5), .col5(switch_3_0_4_output_6),
    .col6(switch_3_0_4_output_7), .col7(switch_3_0_4_output_8), .col8(switch_3_0_4_output_9));
  Button T (.out(btT));
  Button U (.out(btU));
  Button Y (.out(btY));
  Button R (.out(btR));
  Button F (.out(btF));
  Button G (.out(btG));
  Button J (.out(btJ));
  Button H (.out(btH));
  Button V (.out(btV));
  Button B (.out(btB));
  Button C (.out(btC));
  Button N (.out(btN));
  and and_1 (and_1_out, ldf, ~halt);  // AND_Gate
  Transistor #(.\type ("n"), .width(5)) transistor_9 (.in(5'b00100), .out(bt), .gate(btD));
  Transistor #(.\type ("n"), .width(5)) transistor_10 (.in(5'b00101), .out(bt), .gate(btE));
  buf buffer_7 (kcl, btD);
  Transistor #(.\type ("n"), .width(5)) transistor_11 (.in(5'b10010), .out(bt), .gate(btR));
  Transistor #(.\type ("n"), .width(5)) transistor_12 (.in(5'b10001), .out(bt), .gate(btQ));
  buf buffer_8 (kcl, btQ);
  Switch_3_0 switch_3_0_5 (
    .ctrl(r0[3]), .GOLet(5'b01111), .Let(wrd), .Output(switch_3_0_5_output),
    .Output_2(switch_3_0_5_output_2), .Output_3(switch_3_0_5_output_3), .Output_4(switch_3_0_5_output_4),
    .Output_5(switch_3_0_5_output_5), .Output_6(switch_3_0_5_output_6), .Output_7(switch_3_0_5_output_7),
    .Output_8(switch_3_0_5_output_8), .Output_9(switch_3_0_5_output_9), .clock(n3_1_out), .reset(reset),
    .Win(WIN), .WINLet(5'b10111), .Game_over(GO));
  DotMatrix #(.matrixcols(9), .matrixrows(9)) dotmatrix_5 (
    .col0(switch_3_0_5_output), .col1(switch_3_0_5_output_2), .col2(switch_3_0_5_output_3),
    .col3(switch_3_0_5_output_4), .col4(switch_3_0_5_output_5), .col5(switch_3_0_5_output_6),
    .col6(switch_3_0_5_output_7), .col7(switch_3_0_5_output_8), .col8(switch_3_0_5_output_9));
  _4 u_4_1 (.out(n4_1_out), .clock(ld), .adr(adr));
  Button P (.out(btP));
  Button O (.out(btO));
  Button I (.out(btI));
  Button K (.out(btK));
  Button L (.out(btL));
  Button M (.out(btM));
  // Probe on cdm_8_mark5_1_r2
  // Probe on cdm_8_mark5_1_pc
  // Probe on cdm_8_mark5_1_r3
  // Probe on cdm_8_mark5_1_r1
  Transistor #(.\type ("n")) transistor_13 (.in(cl), .out(transistor_13_out), .gate(and_1_out));
  Transistor #(.\type ("n"), .width(5)) transistor_14 (.in(5'b00110), .out(bt), .gate(btF));
  buf buffer_9 (kcl, btE);
  buf buffer_10 (kcl, btF);
  Transistor #(.\type ("n"), .width(5)) transistor_15 (.in(5'b10011), .out(bt), .gate(btS));
  buf buffer_11 (kcl, btS);
  buf buffer_12 (kcl, btR);
  DotMatrix #(.matrixcols(9), .matrixrows(9)) dotmatrix_6 (
    .col0(switch_3_0_6_output), .col1(switch_3_0_6_output_2), .col2(switch_3_0_6_output_3),
    .col3(switch_3_0_6_output_4), .col4(switch_3_0_6_output_5), .col5(switch_3_0_6_output_6),
    .col6(switch_3_0_6_output_7), .col7(switch_3_0_6_output_8), .col8(switch_3_0_6_output_9));
  Switch_3_0 switch_3_0_6 (
    .ctrl(r0[2]), .GOLet(5'b10110), .Let(wrd), .Output(switch_3_0_6_output),
    .Output_2(switch_3_0_6_output_2), .Output_3(switch_3_0_6_output_3), .Output_4(switch_3_0_6_output_4),
    .Output_5(switch_3_0_6_output_5), .Output_6(switch_3_0_6_output_6), .Output_7(switch_3_0_6_output_7),
    .Output_8(switch_3_0_6_output_8), .Output_9(switch_3_0_6_output_9), .clock(n2_1_out), .reset(reset),
    .Win(WIN), .WINLet(5'b01001), .Game_over(GO));
  _3 u_3_1 (.out(n3_1_out), .clock(ld), .adr(adr));
  LED led_1 (.in(halt));
  Button u_Enter (.out(enter));
  // Probe on cdm_8_mark5_1_ps
  // Probe on cdm_8_mark5_1_sp
  CdM_8_mark5 cdm_8_mark5_1 (
    .clock(transistor_13_out), .addr(cdm_8_mark5_1_addr), .mem_read(rd_wr),
    .mem_cycle(cdm_8_mark5_1_mem_cycle), .data_inst(cdm_8_mark5_1_data_inst),
    .data_out(cdm_8_mark5_1_data_out), .data_in(controlled_buffer_2_out), .r0(r0), .r1(cdm_8_mark5_1_r1),
    .r2(cdm_8_mark5_1_r2), .r3(cdm_8_mark5_1_r3), .PC(cdm_8_mark5_1_pc), .SP(cdm_8_mark5_1_sp),
    .PS(cdm_8_mark5_1_ps), .halt(halt), .Start(enter), .Reset(reset));  // open: IAck, IRQ, vec
  Transistor #(.\type ("n"), .width(5)) transistor_16 (.in(5'b00111), .out(bt), .gate(btG));
  buf buffer_13 (kcl, btG);
  Transistor #(.\type ("n"), .width(5)) transistor_17 (.in(5'b10100), .out(bt), .gate(btT));
  buf buffer_14 (kcl, btT);
  _2 u_2_1 (.out(n2_1_out), .clock(ld), .adr(adr));
  DotMatrix #(.matrixcols(9), .matrixrows(9)) dotmatrix_7 (
    .col0(basic_switch_1_output), .col1(basic_switch_1_output_2), .col2(basic_switch_1_output_3),
    .col3(basic_switch_1_output_4), .col4(basic_switch_1_output_5), .col5(basic_switch_1_output_6),
    .col6(basic_switch_1_output_7), .col7(basic_switch_1_output_8), .col8(basic_switch_1_output_9));
  Basic_switch basic_switch_1 (
    .Let(\let ), .Output(basic_switch_1_output), .Output_2(basic_switch_1_output_2),
    .Output_3(basic_switch_1_output_3), .Output_4(basic_switch_1_output_4),
    .Output_5(basic_switch_1_output_5), .Output_6(basic_switch_1_output_6),
    .Output_7(basic_switch_1_output_7), .Output_8(basic_switch_1_output_8), .Output_9(basic_switch_1_output_9));
  assign controlled_buffer_1_out = not_1_out ? cdm_8_mark5_1_data_out : 8'bz;  // Controlled_Buffer controlled_buffer_1
  not not_1 (not_1_out, rd_wr);
  assign controlled_buffer_2_out = rd_wr ? controlled_buffer_1_out : 8'bz;  // Controlled_Buffer controlled_buffer_2
  Transistor #(.\type ("n"), .width(5)) transistor_18 (.in(5'b01000), .out(bt), .gate(btH));
  Transistor #(.\type ("n"), .width(5)) transistor_19 (.in(5'b01001), .out(bt), .gate(btI));
  buf buffer_15 (kcl, btH);
  Transistor #(.\type ("n"), .width(5)) transistor_20 (.in(5'b10101), .out(bt), .gate(btU));
  Transistor #(.\type ("n"), .width(5)) transistor_21 (.in(5'b10110), .out(bt), .gate(btV));
  buf buffer_16 (kcl, btU);
  DotMatrix #(.matrixcols(9), .matrixrows(9)) dotmatrix_8 (
    .col0(switch_3_0_7_output), .col1(switch_3_0_7_output_2), .col2(switch_3_0_7_output_3),
    .col3(switch_3_0_7_output_4), .col4(switch_3_0_7_output_5), .col5(switch_3_0_7_output_6),
    .col6(switch_3_0_7_output_7), .col7(switch_3_0_7_output_8), .col8(switch_3_0_7_output_9));
  Switch_3_0 switch_3_0_7 (
    .ctrl(r0[1]), .GOLet(5'b00101), .Let(wrd), .Output(switch_3_0_7_output),
    .Output_2(switch_3_0_7_output_2), .Output_3(switch_3_0_7_output_3), .Output_4(switch_3_0_7_output_4),
    .Output_5(switch_3_0_7_output_5), .Output_6(switch_3_0_7_output_6), .Output_7(switch_3_0_7_output_7),
    .Output_8(switch_3_0_7_output_8), .Output_9(switch_3_0_7_output_9), .clock(n1_1_out), .reset(reset),
    .Win(WIN), .WINLet(5'b01110), .Game_over(GO));
  _1 u_1_1 (.out(n1_1_out), .clock(ld), .adr(adr));
  Pull_Resistor pull_resistor_3 (.node(code));
  Pull_Resistor pull_resistor_4 (.node(data));
  Decoder decoder_1 (.out0(code), .out1(data), .sel(cdm_8_mark5_1_data_inst), .en(cdm_8_mark5_1_mem_cycle));
  RAM_adress_controller ram_adress_controller_1 (
    .proc(cdm_8_mark5_1_addr), .word_load(adr), .out(ram_adress_controller_1_out), .word_loaded(ldf),
    .halt(halt));
  Transistor #(.\type ("n"), .width(5)) transistor_22 (.in(5'b01010), .out(bt), .gate(btJ));
  buf buffer_17 (kcl, btJ);
  buf buffer_18 (kcl, btI);
  Transistor #(.\type ("n"), .width(5)) transistor_23 (.in(5'b10111), .out(bt), .gate(btW));
  buf buffer_19 (kcl, btW);
  buf buffer_20 (kcl, btV);
  Switch_3_0 switch_3_0_8 (
    .ctrl(r0[0]), .GOLet(5'b10010), .Let(wrd), .Output(switch_3_0_8_output),
    .Output_2(switch_3_0_8_output_2), .Output_3(switch_3_0_8_output_3), .Output_4(switch_3_0_8_output_4),
    .Output_5(switch_3_0_8_output_5), .Output_6(switch_3_0_8_output_6), .Output_7(switch_3_0_8_output_7),
    .Output_8(switch_3_0_8_output_8), .Output_9(switch_3_0_8_output_9), .clock(n0_1_out), .reset(reset),
    .Win(WIN), .WINLet(5'b11011), .Game_over(GO));
  DotMatrix #(.matrixcols(9), .matrixrows(9)) dotmatrix_9 (
    .col0(switch_3_0_8_output), .col1(switch_3_0_8_output_2), .col2(switch_3_0_8_output_3),
    .col3(switch_3_0_8_output_4), .col4(switch_3_0_8_output_5), .col5(switch_3_0_8_output_6),
    .col6(switch_3_0_8_output_7), .col7(switch_3_0_8_output_8), .col8(switch_3_0_8_output_9));
  and and_2 (and_2_out, ~halt, ldf, rd_wr);  // AND_Gate
  or or_2 (or_2_out, data, ~ldf, halt);  // OR_Gate
  Transistor #(.\type ("n"), .width(5)) transistor_24 (.in(5'b01011), .out(bt), .gate(btK));
  buf buffer_21 (kcl, btK);
  Transistor #(.\type ("n"), .width(5)) transistor_25 (.in(5'b11000), .out(bt), .gate(btX));
  buf buffer_22 (kcl, btX);
  _0 u_0_1 (.out(n0_1_out), .clock(ld), .adr(adr));
  ROM rom_2 (.addr(cdm_8_mark5_1_addr), .data(rom_2_data), .sel(code));
  RAM ram_1 (
    .addr(ram_adress_controller_1_out), .data(controlled_buffer_1_out), .sel(or_2_out), .clk(cl),
    .ld(and_2_out), .clr(reset));
  Transistor #(.\type ("n"), .width(5)) transistor_26 (.in(5'b01101), .out(bt), .gate(btM));
  Transistor #(.\type ("n"), .width(5)) transistor_27 (.in(5'b01100), .out(bt), .gate(btL));
  buf buffer_23 (kcl, btL);
  Transistor #(.\type ("n"), .width(5)) transistor_28 (.in(5'b11001), .out(bt), .gate(btY));
  Transistor #(.\type ("n"), .width(5)) transistor_29 (.in(5'b11010), .out(bt), .gate(btZ));
  buf buffer_24 (kcl, btY);
  RAM_data_controller ram_data_controller_1 (
    .out(controlled_buffer_1_out), .proc(rom_2_data), .word(wrd), .letter(\let ), .word_loaded(ldf),
    .halt(halt));
  buf buffer_25 (kcl, btM);
  buf buffer_26 (kcl, btZ);

  // Notes on the sheet:
  //   LIVES
  //   Keyboard
  //   controller
  //   Clock & adress block
  //   Dictionary block
  //   buffer_1 drives only 1 and floats otherwise
  //   buffer_2 drives only 1 and floats otherwise
  //   buffer_3 drives only 1 and floats otherwise
  //   buffer_4 drives only 1 and floats otherwise
  //   contents of rom_1 (hex, n*v repeats v):
  //   1 2 13 f c 15 14 5 3 1 c 5 e 4 1 12 5 c 5 10 8 1 e 14 d f 15 e 14 1 9 e 10 1 12 1 4 9 13 5 15 c 14 9
  //   d 1 14 5 4 f 3 15 d 5 e 14 18 5 e f 10 8 f 2 3 f d 10 15 14 5 12 5 e 7 9 e 5 5 12 6 5 13 14 9 16 1 c
  //   4 9 13 3 f 16 5 12 e 1 16 9 7 1 14 5 f 10 5 12 1 14 f 12 7 5 e 5 12 1 14 5 10 9 3 14 15 12 5 13 2 15
  //   9 c 4 9 e 7 3 8 9 c 4 12 5 e 8 f 13 10 9 14 1 c b 9 14 3 8 5 e 13 c 1 e 7 15 1 7 5 d 9 13 14 1 b 5
  //   13 e f 14 5 2 f f b 10 1 e 14 9 e 7 7 11 15 5 13 14 9 f e 12 5 13 5 1 12 3 8 13 f 6 14 17 1 12 5 13
  //   14 12 1 14 5 7 19 14 12 1 9 e 9 e 7 16 1 3 1 14 9 f e 1 3 14 9 16 9 14 19 13 14 15 4 5 e 14 13
  //   buffer_5 drives only 1 and floats otherwise
  //   buffer_6 drives only 1 and floats otherwise
  //   When the light is ON, choose the letter and press the Enter button
  //   buffer_7 drives only 1 and floats otherwise
  //   buffer_8 drives only 1 and floats otherwise
  //   Processor & memory blocks
  //   buffer_9 drives only 1 and floats otherwise
  //   buffer_10 drives only 1 and floats otherwise
  //   buffer_11 drives only 1 and floats otherwise
  //   buffer_12 drives only 1 and floats otherwise
  //   buffer_13 drives only 1 and floats otherwise
  //   buffer_14 drives only 1 and floats otherwise
  //   buffer_15 drives only 1 and floats otherwise
  //   buffer_16 drives only 1 and floats otherwise
  //   buffer_17 drives only 1 and floats otherwise
  //   buffer_18 drives only 1 and floats otherwise
  //   buffer_19 drives only 1 and floats otherwise
  //   buffer_20 drives only 1 and floats otherwise
  //   buffer_21 drives only 1 and floats otherwise
  //   buffer_22 drives only 1 and floats otherwise
  //   contents of rom_2 (hex, n*v repeats v):
  //   d1 80 c2 ba a e0 13 d3 9 bf 7b e1 e 54 c6 8e 91 ee 2 d4
  //   buffer_23 drives only 1 and floats otherwise
  //   buffer_24 drives only 1 and floats otherwise
  //   buffer_25 drives only 1 and floats otherwise
  //   buffer_26 drives only 1 and floats otherwise
endmodule

module Alphabet (
);

  DotMatrix #(.matrixcols(9), .matrixrows(9)) dotmatrix_1 (
    .col0({9{1'b0}}), .col1(9'h2), .col2(9'h7e), .col3(9'h90), .col4(9'h92), .col5(9'hfe), .col6(9'h7e),
    .col7(9'h2), .col8({9{1'b0}}));
  DotMatrix #(.matrixcols(9), .matrixrows(9)) dotmatrix_2 (
    .col0({9{1'b0}}), .col1(9'h8), .col2(9'he), .col3(9'hc2), .col4(9'h82), .col5(9'hfe), .col6(9'hfc),
    .col7(9'h80), .col8({9{1'b0}}));
  DotMatrix #(.matrixcols(9), .matrixrows(9)) dotmatrix_3 (
    .col0({9{1'b0}}), .col1(9'h64), .col2(9'hf4), .col3(9'h92), .col4(9'h92), .col5(9'h92), .col6(9'hde),
    .col7(9'h4c), .col8({9{1'b0}}));
  DotMatrix #(.matrixcols(9), .matrixrows(9)) dotmatrix_4 (
    .col0({9{1'b0}}), .col1(9'h82), .col2(9'hfe), .col3(9'hfe), .col4(9'h92), .col5(9'h92), .col6(9'hfe),
    .col7(9'h6c), .col8({9{1'b0}}));
  DotMatrix #(.matrixcols(9), .matrixrows(9)) dotmatrix_5 (
    .col0({9{1'b0}}), .col1(9'h82), .col2(9'hfe), .col3(9'hfe), .col4(9'h92), .col5(9'h30), .col6(9'hde),
    .col7(9'h82), .col8({9{1'b0}}));
  DotMatrix #(.matrixcols(9), .matrixrows(9)) dotmatrix_6 (
    .col0({9{1'b0}}), .col1(9'hc0), .col2(9'h82), .col3(9'hfe), .col4(9'hfe), .col5(9'h82), .col6(9'hc0),
    .col7(9'hc0), .col8({9{1'b0}}));
  DotMatrix #(.matrixcols(9), .matrixrows(9)) dotmatrix_7 (
    .col0({9{1'b0}}), .col1(9'h7c), .col2(9'hfe), .col3(9'h82), .col4(9'h82), .col5(9'h82), .col6(9'hc6),
    .col7(9'h64), .col8({9{1'b0}}));
  DotMatrix #(.matrixcols(9), .matrixrows(9)) dotmatrix_8 (
    .col0({9{1'b0}}), .col1(9'h82), .col2(9'hfe), .col3(9'hfe), .col4(9'h2), .col5(9'h2), .col6(9'h2),
    .col7(9'he), .col8({9{1'b0}}));
  DotMatrix #(.matrixcols(9), .matrixrows(9)) dotmatrix_9 (
    .col0({9{1'b0}}), .col1(9'h80), .col2(9'hfc), .col3(9'h6), .col4(9'h86), .col5(9'hfe), .col6(9'hfc),
    .col7(9'h80), .col8({9{1'b0}}));
  DotMatrix #(.matrixcols(9), .matrixrows(9)) dotmatrix_10 (
    .col0({9{1'b0}}), .col1({9{1'b0}}), .col2({9{1'b0}}), .col3({9{1'b0}}), .col4(9'hfa), .col5(9'hfa),
    .col6({9{1'b0}}), .col7({9{1'b0}}), .col8({9{1'b0}}));
  DotMatrix #(.matrixcols(9), .matrixrows(9)) dotmatrix_11 (
    .col0({9{1'b0}}), .col1(9'h82), .col2(9'hfe), .col3(9'hfe), .col4(9'h82), .col5(9'h82), .col6(9'hfe),
    .col7(9'h7c), .col8({9{1'b0}}));
  DotMatrix #(.matrixcols(9), .matrixrows(9)) dotmatrix_12 (
    .col0({9{1'b0}}), .col1(9'hfe), .col2(9'hfe), .col3(9'h22), .col4(9'h10), .col5(9'h60), .col6(9'hfe),
    .col7(9'hfe), .col8({9{1'b0}}));
  DotMatrix #(.matrixcols(9), .matrixrows(9)) dotmatrix_13 (
    .col0({9{1'b0}}), .col1(9'he0), .col2(9'h18), .col3(9'h6), .col4(9'h9e), .col5(9'hf8), .col6(9'he0),
    .col7(9'h80), .col8({9{1'b0}}));
  DotMatrix #(.matrixcols(9), .matrixrows(9)) dotmatrix_14 (
    .col0({9{1'b0}}), .col1(9'h82), .col2(9'hfe), .col3(9'hfe), .col4(9'h92), .col5(9'h92), .col6(9'h82),
    .col7(9'hc6), .col8({9{1'b0}}));
  DotMatrix #(.matrixcols(9), .matrixrows(9)) dotmatrix_15 (
    .col0({9{1'b0}}), .col1(9'hfe), .col2(9'hfe), .col3(9'h60), .col4(9'h10), .col5(9'hc), .col6(9'hfe),
    .col7(9'hfe), .col8({9{1'b0}}));
  DotMatrix #(.matrixcols(9), .matrixrows(9)) dotmatrix_16 (
    .col0({9{1'b0}}), .col1(9'hf8), .col2(9'he), .col3(9'h30), .col4(9'h78), .col5(9'hc), .col6(9'hfe),
    .col7(9'hf8), .col8({9{1'b0}}));
  DotMatrix #(.matrixcols(9), .matrixrows(9)) dotmatrix_17 (
    .col0({9{1'b0}}), .col1(9'h30), .col2(9'h22), .col3(9'hfe), .col4(9'hf8), .col5(9'hfe), .col6(9'h22),
    .col7(9'h30), .col8({9{1'b0}}));
  DotMatrix #(.matrixcols(9), .matrixrows(9)) dotmatrix_18 (
    .col0({9{1'b0}}), .col1(9'h60), .col2(9'h22), .col3(9'hfe), .col4(9'hf8), .col5(9'hfe), .col6(9'h22),
    .col7(9'h60), .col8({9{1'b0}}));
  DotMatrix #(.matrixcols(9), .matrixrows(9)) dotmatrix_19 (
    .col0({9{1'b0}}), .col1(9'h82), .col2(9'hfe), .col3(9'hfe), .col4(9'h92), .col5(9'h90), .col6(9'h80),
    .col7(9'hc0), .col8({9{1'b0}}));
  DotMatrix #(.matrixcols(9), .matrixrows(9)) dotmatrix_20 (
    .col0({9{1'b0}}), .col1(9'h7c), .col2(9'hfe), .col3(9'h82), .col4(9'h82), .col5(9'h82), .col6(9'hfe),
    .col7(9'h7c), .col8({9{1'b0}}));
  DotMatrix #(.matrixcols(9), .matrixrows(9)) dotmatrix_21 (
    .col0({9{1'b0}}), .col1(9'h82), .col2(9'hc6), .col3(9'h28), .col4(9'h10), .col5(9'hee), .col6(9'hc6),
    .col7(9'h82), .col8({9{1'b0}}));
  DotMatrix #(.matrixcols(9), .matrixrows(9)) dotmatrix_22 (
    .col0({9{1'b0}}), .col1(9'h7c), .col2(9'hfe), .col3(9'h82), .col4(9'h92), .col5(9'h9e), .col6(9'hde),
    .col7(9'h50), .col8({9{1'b0}}));
  DotMatrix #(.matrixcols(9), .matrixrows(9)) dotmatrix_23 (
    .col0({9{1'b0}}), .col1(9'h82), .col2(9'hfe), .col3(9'hfe), .col4(9'h8a), .col5(9'h88), .col6(9'hf8),
    .col7(9'h70), .col8({9{1'b0}}));
  DotMatrix #(.matrixcols(9), .matrixrows(9)) dotmatrix_24 (
    .col0({9{1'b0}}), .col1(9'h80), .col2(9'he0), .col3(9'h22), .col4(9'h9e), .col5(9'hfe), .col6(9'he2),
    .col7(9'h80), .col8({9{1'b0}}));
  DotMatrix #(.matrixcols(9), .matrixrows(9)) dotmatrix_25 (
    .col0({9{1'b0}}), .col1(9'h30), .col2(9'h20), .col3(9'hfe), .col4(9'hf8), .col5(9'hfe), .col6(9'h22),
    .col7(9'h20), .col8({9{1'b0}}));
  DotMatrix #(.matrixcols(9), .matrixrows(9)) dotmatrix_26 (
    .col0({9{1'b1}}), .col1(9'h118), .col2(9'h110), .col3(9'h17f), .col4(9'h17c), .col5(9'h17f),
    .col6(9'h111), .col7(9'h110), .col8({9{1'b1}}));
  DotMatrix #(.matrixcols(9), .matrixrows(9)) dotmatrix_27 (
    .col0({9{1'b0}}), .col1(9'h82), .col2(9'hfe), .col3(9'h92), .col4(9'h10), .col5(9'hfe), .col6(9'hfe),
    .col7(9'h82), .col8({9{1'b0}}));
  DotMatrix #(.matrixcols(9), .matrixrows(9)) dotmatrix_28 (
    .col0({9{1'b0}}), .col1(9'h7c), .col2(9'hfe), .col3(9'h82), .col4(9'h88), .col5(9'h86), .col6(9'hfe),
    .col7(9'h7a), .col8({9{1'b0}}));
  DotMatrix #(.matrixcols(9), .matrixrows(9)) dotmatrix_29 (
    .col0({9{1'b0}}), .col1(9'he2), .col2(9'h86), .col3(9'h8e), .col4(9'h92), .col5(9'he2), .col6(9'hc2),
    .col7(9'h8e), .col8({9{1'b0}}));
  DotMatrix #(.matrixcols(9), .matrixrows(9)) dotmatrix_30 (
    .col0({9{1'b0}}), .col1(9'hc6), .col2(9'h82), .col3(9'hfe), .col4(9'hfe), .col5(9'h82), .col6(9'hc6),
    .col7(9'hc6), .col8({9{1'b0}}));
  DotMatrix #(.matrixcols(9), .matrixrows(9)) dotmatrix_31 (
    .col0({9{1'b0}}), .col1(9'hfe), .col2(9'hfe), .col3(9'h92), .col4(9'h98), .col5(9'h98), .col6(9'hf6),
    .col7(9'h62), .col8({9{1'b0}}));
  DotMatrix #(.matrixcols(9), .matrixrows(9)) dotmatrix_32 (
    .col0({9{1'b0}}), .col1(9'h7f), .col2(9'ha4), .col3({9{1'b1}}), .col4(9'h124), .col5({9{1'b1}}),
    .col6(9'ha4), .col7(9'h7f), .col8({9{1'b0}}));
  DotMatrix #(.matrixcols(9), .matrixrows(9)) dotmatrix_33 (
    .col0({9{1'b0}}), .col1(9'h7f), .col2(9'h80), .col3(9'h100), .col4(9'h100), .col5(9'h100), .col6(9'h80),
    .col7(9'h7f), .col8({9{1'b0}}));
endmodule

module answers (
);


  // Notes on the sheet:
  //   50) FESTIVAL; DISCOVER
  //   70) GENERATE; BEAUTIFY
  //   80) BUILDING; CHILDREN
  //   90) HOSPITAL; KITCHEN
  //   a0) LANGUAGE; MISTAKES
  //   b0) NOTEBOOK; PAINTING
  //   c0) QUESTION; RECEARCH
  //   d0)SOFTWARE; STRATEGY
  //   e0)TRAINING; VACATION
  //   d0)ACTIVITY; STUDENTS
  //   00) ABSOLUTE; CALENDAR
  //   10) ELEPHANT; MOUNTAIN
  //   20) PARADISE; ULTIMATE 
  //   30) PICTURES; XENOPHOB
  //   40) COMPUTER; ENGINEER
  //   60) NAVIGATE; OPERATOR
endmodule

module Basic_switch (
  input  [4:0] Let,
  output [8:0] Output,
  output [8:0] Output_2,
  output [8:0] Output_3,
  output [8:0] Output_4,
  output [8:0] Output_5,
  output [8:0] Output_6,
  output [8:0] Output_7,
  output [8:0] Output_8,
  output [8:0] Output_9
);

  Multiplexer #(.select(5), .width(27), .enable("false")) multiplexer_1 (
    .in0({27{1'b0}}), .in1(27'h47e), .in2(27'h104fe), .in3(27'hf8fe), .in4(27'h104fe), .in5(27'h104fe),
    .in6(27'h104fe), .in7(27'hf8fe), .in8(27'h104fe), .in9(27'h18c82), .in10(27'h100e), .in11(27'h104fe),
    .in12(27'h104fe), .in13(27'h1fcfe), .in14(27'h1fcfe), .in15(27'hf8fe), .in16(27'h104fe), .in17(27'hf8fe),
    .in18(27'h1fcfe), .in19(27'hc8f4), .in20(27'h18082), .in21(27'h100fc), .in22(27'h1c018),
    .in23(27'h1f00e), .in24(27'h104c6), .in25(27'h100e0), .in26(27'h1c486), .in27({27{1'b0}}),
    .in28({27{1'b0}}), .in29({27{1'b0}}), .in30({27{1'b0}}), .in31({27{1'b0}}),
    .out({Output, Output_2, Output_3}), .sel(Let));
  Multiplexer #(.select(5), .width(27), .enable("false")) multiplexer_2 (
    .in0({27{1'b0}}), .in1(27'h24124fe), .in2(27'h3f92492), .in3(27'h2090482), .in4(27'h3f90482),
    .in5(27'h3f92492), .in6(27'h3f92490), .in7(27'h209249e), .in8(27'h24820fe), .in9(27'h3f9fc82),
    .in10(27'h30904fe), .in11(27'h3f92430), .in12(27'h3f80402), .in13(27'h882060), .in14(27'h180200c),
    .in15(27'h2090482), .in16(27'h3f91488), .in17(27'h2091086), .in18(27'h2493098), .in19(27'h2492492),
    .in20(27'h3f9fc82), .in21(27'h190cfe), .in22(27'h193cf8), .in23(27'hc0f00c), .in24(27'ha020ee),
    .in25(27'h893cfe), .in26(27'h23924e2), .in27({27{1'b0}}), .in28({27{1'b0}}), .in29({27{1'b0}}),
    .in30({27{1'b0}}), .in31({27{1'b0}}), .out({Output_4, Output_5, Output_6}), .sel(Let));
  Multiplexer #(.select(5), .width(27), .enable("false")) multiplexer_3 (
    .in0({27{1'b0}}), .in1(27'h1f80400), .in2(27'h3f8d800), .in3(27'h318c800), .in4(27'h3f8f800),
    .in5(27'h2098c00), .in6(27'h2018000), .in7(27'h378a000), .in8(27'h3f90400), .in9(27'h3198c00),
    .in10(27'h3f10000), .in11(27'h3790400), .in12(27'h81c00), .in13(27'h3f9fc00), .in14(27'h3f9fc00),
    .in15(27'h3f8f800), .in16(27'h3e0e000), .in17(27'h3f8f400), .in18(27'h3d8c400), .in19(27'h3789800),
    .in20(27'h3018000), .in21(27'h3f10000), .in22(27'h3810000), .in23(27'h3f9f000), .in24(27'h3190400),
    .in25(27'h3890000), .in26(27'h3091c00), .in27({27{1'b0}}), .in28({27{1'b0}}), .in29({27{1'b0}}),
    .in30({27{1'b0}}), .in31({27{1'b0}}), .out({Output_7, Output_8, Output_9}), .sel(Let));
endmodule

module Switch_3_0 (
  input  ctrl,
  input  [4:0] Let,
  input  [4:0] GOLet,
  input  [4:0] WINLet,
  input  reset,
  input  clock,
  input  Win,
  input  Game_over,
  output [8:0] Output,
  output [8:0] Output_2,
  output [8:0] Output_3,
  output [8:0] Output_4,
  output [8:0] Output_5,
  output [8:0] Output_6,
  output [8:0] Output_7,
  output [8:0] Output_8,
  output [8:0] Output_9
);

  wire clock_1_out, comparator_1_eq, multiplexer_1_out, multiplexer_4_out;
  wire [1:1] done;
  wire [4:0] let_t, multiplexer_3_out;
  wire [7:0] counter_1_q;
  wire [8:0] multiplexer_2_out, multiplexer_2_out_2, multiplexer_2_out_3, multiplexer_5_out,
       multiplexer_5_out_2, multiplexer_5_out_3, multiplexer_6_out, multiplexer_6_out_2, multiplexer_6_out_3;

  Transistor #(.\type ("n"), .width(9)) transistor_1 (.in(multiplexer_2_out_3), .out(Output), .gate(multiplexer_1_out));
  Multiplexer #(.select(2), .enable("false")) multiplexer_1 (
    .in0(ctrl), .in1(1'b1), .in2(1'b1), .in3(1'b1), .out(multiplexer_1_out), .sel({done[1], Game_over}));
  Counter_part counter_1 (.count(Win), .Q(counter_1_q), .clk(clock_1_out));  // open: load, D, carry, clr
  Clock clock_1 (.out(clock_1_out));
  Transistor #(.\type ("n"), .width(9)) transistor_2 (
    .in(multiplexer_2_out_2), .out(Output_2), .gate(multiplexer_1_out));
  Multiplexer #(.select(5), .width(27), .enable("false")) multiplexer_2 (
    .in0({27{1'b0}}), .in1(27'h47e), .in2(27'h104fe), .in3(27'hf8fe), .in4(27'h104fe), .in5(27'h104fe),
    .in6(27'h104fe), .in7(27'hf8fe), .in8(27'h104fe), .in9(27'h18c82), .in10(27'h100e), .in11(27'h104fe),
    .in12(27'h104fe), .in13(27'h1fcfe), .in14(27'h1fcfe), .in15(27'hf8fe), .in16(27'h104fe), .in17(27'hf8fe),
    .in18(27'h1fcfe), .in19(27'hc8f4), .in20(27'h18082), .in21(27'h100fc), .in22(27'h1c018),
    .in23(27'h1f00e), .in24(27'h104c6), .in25(27'h100e0), .in26(27'h1c486), .in27({27{1'b0}}),
    .in28({27{1'b0}}), .in29({27{1'b0}}), .in30({27{1'b0}}), .in31({27{1'b0}}),
    .out({multiplexer_2_out_3, multiplexer_2_out_2, multiplexer_2_out}), .sel(let_t));
  Comparator comparator_1 (.a(counter_1_q), .b({8{1'b1}}), .eq(comparator_1_eq));  // open: gt, lt
  assign done[1] = comparator_1_eq ? Win : 1'bz;  // Controlled_Buffer controlled_buffer_1
  Pull_Resistor pull_resistor_1 (.node(done[1]));
  Transistor #(.\type ("n"), .width(9)) transistor_3 (.in(multiplexer_2_out), .out(Output_3), .gate(multiplexer_1_out));
  Multiplexer #(.select(2), .width(5), .enable("false")) multiplexer_3 (
    .in0(Let), .in1(GOLet), .in2(WINLet), .in3(WINLet), .out(multiplexer_3_out), .sel({done[1], Game_over}));
  Multiplexer #(.select(2), .enable("false")) multiplexer_4 (
    .in0(clock), .in1(1'b1), .in2(1'b1), .in3(1'b1), .out(multiplexer_4_out), .sel({done[1], Game_over}));
  Register #(.width(5)) register_1 (
    .D(multiplexer_3_out), .Q(let_t), .clk(multiplexer_4_out), .clr(reset));  // open: en
  Transistor #(.\type ("n"), .width(9)) transistor_4 (
    .in(multiplexer_5_out_3), .out(Output_4), .gate(multiplexer_1_out));
  Transistor #(.\type ("n"), .width(9)) transistor_5 (
    .in(multiplexer_5_out_2), .out(Output_5), .gate(multiplexer_1_out));
  Multiplexer #(.select(5), .width(27), .enable("false")) multiplexer_5 (
    .in0({27{1'b0}}), .in1(27'h24124fe), .in2(27'h3f92492), .in3(27'h2090482), .in4(27'h3f90482),
    .in5(27'h3f92492), .in6(27'h3f92490), .in7(27'h209249e), .in8(27'h24820fe), .in9(27'h3f9fc82),
    .in10(27'h30904fe), .in11(27'h3f92430), .in12(27'h3f80402), .in13(27'h882060), .in14(27'h180200c),
    .in15(27'h2090482), .in16(27'h3f91488), .in17(27'h2091086), .in18(27'h2493098), .in19(27'h2492492),
    .in20(27'h3f9fc82), .in21(27'h190cfe), .in22(27'h193cf8), .in23(27'hc0f00c), .in24(27'ha020ee),
    .in25(27'h893cfe), .in26(27'h23924e2), .in27(27'h3e9f400), .in28({27{1'b0}}), .in29({27{1'b0}}),
    .in30({27{1'b0}}), .in31({27{1'b0}}),
    .out({multiplexer_5_out_3, multiplexer_5_out_2, multiplexer_5_out}), .sel(let_t));
  Transistor #(.\type ("n"), .width(9)) transistor_6 (.in(multiplexer_5_out), .out(Output_6), .gate(multiplexer_1_out));
  Transistor #(.\type ("n"), .width(9)) transistor_7 (
    .in(multiplexer_6_out_3), .out(Output_7), .gate(multiplexer_1_out));
  Transistor #(.\type ("n"), .width(9)) transistor_8 (
    .in(multiplexer_6_out_2), .out(Output_8), .gate(multiplexer_1_out));
  Multiplexer #(.select(5), .width(27), .enable("false")) multiplexer_6 (
    .in0({27{1'b0}}), .in1(27'h1f80400), .in2(27'h3f8d800), .in3(27'h318c800), .in4(27'h3f8f800),
    .in5(27'h2098c00), .in6(27'h2018000), .in7(27'h378a000), .in8(27'h3f90400), .in9(27'h3198c00),
    .in10(27'h3f10000), .in11(27'h3790400), .in12(27'h81c00), .in13(27'h3f9fc00), .in14(27'h3f9fc00),
    .in15(27'h3f8f800), .in16(27'h3e0e000), .in17(27'h3f8f400), .in18(27'h3d8c400), .in19(27'h3789800),
    .in20(27'h3018000), .in21(27'h3f10000), .in22(27'h3810000), .in23(27'h3f9f000), .in24(27'h3190400),
    .in25(27'h3890000), .in26(27'h3091c00), .in27({27{1'b0}}), .in28({27{1'b0}}), .in29({27{1'b0}}),
    .in30({27{1'b0}}), .in31({27{1'b0}}),
    .out({multiplexer_6_out_3, multiplexer_6_out_2, multiplexer_6_out}), .sel(let_t));
  Transistor #(.\type ("n"), .width(9)) transistor_9 (.in(multiplexer_6_out), .out(Output_9), .gate(multiplexer_1_out));
  Transistor #(.gate("br"), .width(9)) transistor_10 (.in({9{1'b0}}), .out(Output), .gate(multiplexer_1_out));
  Transistor #(.gate("br"), .width(9)) transistor_11 (.in(9'h7f), .out(Output_2), .gate(multiplexer_1_out));
  Transistor #(.gate("br"), .width(9)) transistor_12 (.in(9'ha4), .out(Output_3), .gate(multiplexer_1_out));
  Transistor #(.gate("br"), .width(9)) transistor_13 (.in({9{1'b1}}), .out(Output_4), .gate(multiplexer_1_out));
  Transistor #(.gate("br"), .width(9)) transistor_14 (.in(9'h124), .out(Output_5), .gate(multiplexer_1_out));
  Transistor #(.gate("br"), .width(9)) transistor_15 (.in({9{1'b1}}), .out(Output_6), .gate(multiplexer_1_out));
  Transistor #(.gate("br"), .width(9)) transistor_16 (.in(9'ha4), .out(Output_7), .gate(multiplexer_1_out));
  Transistor #(.gate("br"), .width(9)) transistor_17 (.in(9'h7f), .out(Output_8), .gate(multiplexer_1_out));
  Transistor #(.gate("br"), .width(9)) transistor_18 (.in({9{1'b0}}), .out(Output_9), .gate(multiplexer_1_out));

  // Other names for the same wires on the sheet: done[0] = Game_over
endmodule

module Life_cntr (
  input  start,
  input  [7:0] flags,
  input  clock,
  input  reset,
  output [3:0] display,
  output Game_over
);

  wire comparator_1_eq, d_ff_1_q;
  wire [2:0] counter_1_q;
  wire [7:0] register_1_q;

  Register register_1 (.D(flags), .Q(register_1_q), .clk(clock), .clr(reset));  // open: en
  Comparator comparator_1 (.a(flags), .b(register_1_q), .eq(comparator_1_eq));  // open: gt, lt
  Multiplexer #(.width(4), .enable("false")) multiplexer_1 (
    .in0(4'b0001), .in1({1'b0, counter_1_q}), .out(display), .sel(d_ff_1_q));
  D_Flip_Flop d_ff_1 (.clk(start), .D(start), .Q(d_ff_1_q));  // open: Qn, preset, en, reset
  Counter_part #(.width(3), .max('h7), .ongoal("stay")) counter_1 (
    .count(comparator_1_eq), .Q(counter_1_q), .carry(Game_over), .clk(clock), .clr(reset));  // open: load, D
endmodule

module counter_invertor (
  input  [3:0] \input ,
  output [3:0] \output 
);

  not not_1 (\output [1], \input [1]);
  not not_2 (\output [2], \input [2]);
  not not_3 (\output [0], \input [0]);

  assign \output [3] = \input [3];
endmodule

module Counter (
  input  [7:0] Max,
  input  clock,
  input  reset,
  output \end ,
  output [7:0] out
);

  wire st;
  wire [7:0] inc_1_out;

  inc inc_1 (.in(out), .out(inc_1_out));  // open: cout
  Register register_1 (.D(inc_1_out), .en(st), .Q(out), .clk(clock), .clr(reset));
  Comparator comparator_1 (.a(Max), .b(out), .lt(\end ));  // open: gt, eq
  not not_1 (st, \end );
endmodule

module inc (
  input  [7:0] in,
  output [7:0] out,
  output cout
);

  wire [7:1] and_1_out;

  assign {cout, and_1_out} = {and_1_out, 1'b1} & in;  // AND_Gate and_1, 8 bits wide
  assign out = in ^ {and_1_out, 1'b1};  // XOR_Gate xor_1, 8 bits wide
endmodule

module RAM_adress_controller (
  input  [7:0] proc,
  input  [3:0] word_load,
  input  word_loaded,
  input  halt,
  output [7:0] out
);

  wire [7:0] transistor_1_out, transistor_3_out;

  Transistor #(.\type ("n"), .gate("br"), .width(8)) transistor_1 (
    .in(proc), .out(transistor_1_out), .gate(word_loaded));
  Transistor #(.gate("br"), .width(8)) transistor_2 (.in({4'b0000, word_load}), .out(out), .gate(word_loaded));
  Transistor #(.\type ("n"), .gate("br"), .width(8)) transistor_3 (
    .in(8'h9), .out(transistor_3_out), .gate(word_loaded));
  Transistor #(.gate("br"), .width(8)) transistor_4 (.in(transistor_1_out), .out(out), .gate(halt));
  Transistor #(.\type ("n"), .gate("br"), .width(8)) transistor_5 (.in(transistor_3_out), .out(out), .gate(halt));

  // Notes on the sheet:
  //   letter load
endmodule

module RAM_data_controller (
  input  [7:0] proc,
  input  [4:0] word,
  input  [4:0] letter,
  input  word_loaded,
  input  halt,
  output [7:0] out
);

  wire [7:0] transistor_4_out, transistor_5_out;

  Transistor #(.\type ("n"), .gate("br"), .width(8)) transistor_1 (
    .in(transistor_4_out), .out(out), .gate(word_loaded));
  Transistor #(.gate("br"), .width(8)) transistor_2 (.in({3'b000, word}), .out(out), .gate(word_loaded));
  Transistor #(.\type ("n"), .gate("br"), .width(8)) transistor_3 (
    .in(transistor_5_out), .out(out), .gate(word_loaded));
  Transistor #(.gate("br"), .width(8)) transistor_4 (.in(proc), .out(transistor_4_out), .gate(halt));
  Transistor #(.\type ("n"), .gate("br"), .width(8)) transistor_5 (
    .in({3'b000, letter}), .out(transistor_5_out), .gate(halt));
endmodule
