// Logisim project NSU-2023-T04L1e08.circ as structural Verilog: 1 circuit, main circuit mycircuit
module mycircuit (
  input  A,
  input  B,
  input  C,
  output R
);

  wire nor_1_out;

  nor nor_1 (nor_1_out, A, B, C);
  NotExactlyOne xnor_1 (.out(R), .in0(A), .in1(nor_1_out), .in2(B), .in4(C));
endmodule
