// Logisim project NSU-2023-T04L1e09.circ as structural Verilog: 1 circuit, main circuit mycircuit
module mycircuit (
  input  A,
  input  B,
  input  C,
  output R
);

  and and_1 (R, A, ~C);  // AND_Gate
endmodule
