// Logisim project NSU-2023-T04L1e14.circ as structural Verilog: 1 circuit, main circuit mycircuit
module mycircuit (
  input  A,
  input  B,
  input  C,
  output R
);

  xor xor_1 (R, B, ~C);  // XOR_Gate
endmodule
