// Logisim project NSU-2023-T04L1e16.circ as structural Verilog: 1 circuit, main circuit mycircuit
module mycircuit (
  input  A,
  input  B,
  input  C,
  output R
);

  wire xor_1_out;

  xor xor_1 (xor_1_out, A, C);
  or or_1 (R, xor_1_out, ~C);  // OR_Gate
endmodule
