// Logisim project NSU-2023-T04L2e01.circ as structural Verilog: 1 circuit, main circuit OR3
module OR3 (
  input  A,
  input  B,
  input  C,
  output R
);

  wire transistor_4_out, transistor_5_out;

  Transistor #(.\type ("n")) transistor_1 (.in(1'b0), .out(R), .gate(A));
  Transistor #(.\type ("n")) transistor_2 (.in(1'b0), .out(R), .gate(B));
  Transistor #(.\type ("n"), .gate("br")) transistor_3 (.in(1'b0), .out(R), .gate(C));
  Transistor transistor_4 (.in(1'b1), .out(transistor_4_out), .gate(A));
  Transistor transistor_5 (.in(transistor_4_out), .out(transistor_5_out), .gate(B));
  Transistor transistor_6 (.in(transistor_5_out), .out(R), .gate(C));
endmodule
