// Logisim project NSU-2023-T04L3e01.circ as structural Verilog: 1 circuit, main circuit formula
module formula (
  input  A,
  input  B,
  input  C,
  output R,
  output R_2
);

  wire transistor_2_out, transistor_3_out;

  Transistor #(.\type ("n"), .gate("br")) transistor_1 (.in(transistor_2_out), .out(R_2), .gate(B));
  Transistor #(.\type ("n")) transistor_2 (.in(1'b0), .out(transistor_2_out), .gate(A));
  Transistor #(.\type ("n")) transistor_3 (.in(1'b0), .out(transistor_3_out), .gate(B));
  Transistor #(.\type ("n"), .gate("br")) transistor_4 (.in(transistor_3_out), .out(R_2), .gate(C));
  Transistor #(.\type ("n"), .gate("br")) transistor_5 (.in(1'b0), .out(transistor_3_out), .gate(A));
  Pull_Resistor #(.pull(1)) pull_resistor_1 (.node(R_2));
endmodule
