// Logisim project MyLib.circ as structural Verilog: 5 circuits, main circuit Sum1
module Sum1 (
  input  Cin,
  input  in,
  input  in_2,
  output Out,
  output Cout
);

  wire and_1_out, and_2_out, xor_1_out;

  xor xor_1 (xor_1_out, in, in_2);
  xor xor_2 (Out, xor_1_out, Cin);
  and and_1 (and_1_out, in, in_2);
  or or_1 (Cout, and_1_out, and_2_out);
  and and_2 (and_2_out, xor_1_out, Cin);
endmodule

module Sum8 (
  input  [7:0] in1,
  input  Cin,
  input  [7:0] in2,
  output [7:0] Out,
  output Cout
);

  wire sum1_1_cout, sum1_2_cout, sum1_3_cout, sum1_4_cout, sum1_5_cout, sum1_6_cout, sum1_7_cout;

  Sum1 sum1_1 (.in(in1[0]), .in_2(in2[0]), .Cin(Cin), .Cout(sum1_1_cout), .Out(Out[0]));
  Sum1 sum1_2 (.in(in1[1]), .in_2(in2[1]), .Cin(sum1_1_cout), .Cout(sum1_2_cout), .Out(Out[1]));
  Sum1 sum1_3 (.in(in1[2]), .in_2(in2[2]), .Cin(sum1_2_cout), .Cout(sum1_3_cout), .Out(Out[2]));
  Sum1 sum1_4 (.in(in1[3]), .in_2(in2[3]), .Cin(sum1_3_cout), .Cout(sum1_4_cout), .Out(Out[3]));
  Sum1 sum1_5 (.in(in1[4]), .in_2(in2[4]), .Cin(sum1_4_cout), .Cout(sum1_5_cout), .Out(Out[4]));
  Sum1 sum1_6 (.in(in1[5]), .in_2(in2[5]), .Cin(sum1_5_cout), .Cout(sum1_6_cout), .Out(Out[5]));
  Sum1 sum1_7 (.in(in1[6]), .in_2(in2[6]), .Cin(sum1_6_cout), .Cout(sum1_7_cout), .Out(Out[6]));
  Sum1 sum1_8 (.in(in1[7]), .in_2(in2[7]), .Cin(sum1_7_cout), .Cout(Cout), .Out(Out[7]));
endmodule

module Sum4 (
  input  [3:0] in1,
  input  [3:0] in2,
  output [3:0] Out,
  output Cout
);

  wire sum1_1_cout, sum1_2_cout, sum1_3_cout;

  Sum1 sum1_1 (.in(in1[0]), .in_2(in2[0]), .Cin(1'b0), .Cout(sum1_1_cout), .Out(Out[0]));
  Sum1 sum1_2 (.in(in1[1]), .in_2(in2[1]), .Cin(sum1_1_cout), .Cout(sum1_2_cout), .Out(Out[1]));
  Sum1 sum1_3 (.in(in1[2]), .in_2(in2[2]), .Cin(sum1_2_cout), .Cout(sum1_3_cout), .Out(Out[2]));
  Sum1 sum1_4 (.in(in1[3]), .in_2(in2[3]), .Cin(sum1_3_cout), .Cout(Cout), .Out(Out[3]));
endmodule

module Sub8 (
  input  Cin,
  input  [7:0] in1,
  input  [7:0] out,
  input  [7:0] in2,
  output Cout
);

  wire [7:0] inc_1_r, not_1_out;

  assign not_1_out = ~in2;  // NOT_Gate not_1, 8 bits wide
  inc inc_1 (.X(not_1_out), .R(inc_1_r));  // open: Cout
  Sum8 sum8_1 (.Out(out), .Cout(Cout), .in1(in1), .in2(inc_1_r), .Cin(Cin));
endmodule

module inc (
  input  [7:0] X,
  output [7:0] R,
  output Cout
);

  wire [6:0] and_1_out;

  assign {Cout, and_1_out} = {and_1_out, 1'b1} & X;  // AND_Gate and_1, 8 bits wide
  assign R = X ^ {and_1_out, 1'b1};  // XOR_Gate xor_1, 8 bits wide
endmodule
