// Logisim project NSU-2023-T05L1e11.circ as structural Verilog: 4 circuits, main circuit main
module main (
  input  [7:0] u,
  input  [7:0] v,
  output [7:0] R
);

  wire and_1_out, and_2_out, not_1_out, xor_1_out, xor_2_out;
  wire [7:0] add_1_sum, add_2_sum, mux_1_output;

  inc inc_1 ();  // open: X, R, Cout
  // Probe on u
  // Probe on v
  add add_1 (.A(u), .B(8'h78), .sum(add_1_sum));  // open: Cout, Cin
  add add_2 (.A(v), .B(8'h78), .sum(add_2_sum));  // open: Cout, Cin
  xor xor_1 (xor_1_out, u[7], add_1_sum[7]);
  and and_1 (and_1_out, xor_1_out, add_1_sum[7]);
  MUX mux_1 (.Input_0(add_1_sum), .sel(and_1_out), .Input_1(add_2_sum), .Output(mux_1_output));
  and and_2 (and_2_out, add_2_sum[7], xor_2_out);
  xor xor_2 (xor_2_out, add_2_sum[7], v[7]);
  MUX mux_2 ();  // open: Input_0, sel, Input_1, Output
  MUX mux_3 (.Input_0(mux_1_output), .sel(and_2_out), .Input_1(8'h78), .Output(R));
  // Probe on R
  add add_3 ();  // open: A, B, sum, Cout, Cin
  not not_1 (not_1_out, not_1_out);
  // NOT_Gate not_2 is placed but not wired
  // OR_Gate or_1 is placed but not wired
  // OR_Gate or_2 is placed but not wired
  // AND_Gate and_3 is placed but not wired
  // AND_Gate and_4 is placed but not wired
  // XOR_Gate xor_3 is placed but not wired
  // XOR_Gate xor_4 is placed but not wired
  // XNOR_Gate xnor_1 is placed but not wired

  // Notes on the sheet:
  //   signed decimal:
  //   signed decimal:
  //   split a bunch into 8 individual wires
  //   all the above are 8-bit devices
  //   You are only allowed to use Wiring and Gates libraries
  //   Chips you may use in addition to gates (Click and Ctrl/D duplicates):
  //   You may also use the following (and any other)  splitters facing any direction
  //   ATTENTION! DO NOT MOVE ANY PINS!
  //   Ignore overflow, unless instructed otherwise
  //   You may build and use your own chips using gates and wires
  //   out = A if sel=0
  //   B if sel=1
  //   signed decimal:
  //   extract the sign bit (bit 7) from an 8-bit bunch
  //   extract the LSB  (bit 0) from an 8-bit bunch
  //   constant 8-bit value (change it to anything  you want)
  //   Cin pulled to 0 if disconnected
  //   Gates: Click and Ctrl/D duplicates
  //   You may use any gates, not just the above ones
endmodule

module inc (
  input  [7:0] X,
  output [7:0] R,
  output Cout
);

  wire [7:1] and_1_out;

  assign {Cout, and_1_out} = {and_1_out, 1'b1} & X;  // AND_Gate and_1, 8 bits wide
  assign R = X ^ {and_1_out, 1'b1};  // XOR_Gate xor_1, 8 bits wide
endmodule

module add (
  input  [7:0] A,
  input  [7:0] B,
  input  Cin,
  output [7:0] sum,
  output Cout
);

  wire [6:0] or_1_out;
  wire [7:0] and_1_out, and_2_out, and_3_out;

  Pull_Resistor pull_resistor_1 (.node(Cin));
  assign and_1_out = A & B;  // AND_Gate and_1, 8 bits wide
  assign and_2_out = B & {or_1_out, Cin};  // AND_Gate and_2, 8 bits wide
  assign and_3_out = A & {or_1_out, Cin};  // AND_Gate and_3, 8 bits wide
  assign {Cout, or_1_out} = and_1_out | and_2_out | and_3_out;  // OR_Gate or_1, 8 bits wide
  assign sum = A ^ {or_1_out, Cin} ^ B;  // XOR_Gate xor_1, 8 bits wide
endmodule

module MUX (
  input  [7:0] Input_0,
  input  sel,
  input  [7:0] Input_1,
  output [7:0] Output
);

  wire [7:0] and_1_out, and_2_out;
  wire [7:7] not_1_out;

  not not_1 (not_1_out[7], sel);
  assign and_1_out = Input_0 & {8{not_1_out[7]}};  // AND_Gate and_1, 8 bits wide
  assign and_2_out = {8{sel}} & Input_1;  // AND_Gate and_2, 8 bits wide
  assign Output = and_1_out | and_2_out;  // OR_Gate or_1, 8 bits wide
endmodule
