// Logisim project NSU-2023-T05L2e02.circ as structural Verilog: 1 circuit, main circuit dec
module dec (
  input  [7:0] X,
  output [7:0] R,
  output Cout
);

  wire [6:0] and_1_out;
  wire [7:0] not_1_out, xor_1_out;

  assign not_1_out = ~X;  // NOT_Gate not_1, 8 bits wide
  assign {Cout, and_1_out} = {and_1_out, 1'b1} & not_1_out;  // AND_Gate and_1, 8 bits wide
  assign xor_1_out = not_1_out ^ {and_1_out, 1'b1};  // XOR_Gate xor_1, 8 bits wide
  assign R = ~xor_1_out;  // NOT_Gate not_2, 8 bits wide
endmodule
