// Logisim project NSU-2023-T05L2e03.circ as structural Verilog: 1 circuit, main circuit formula
module formula (
  input  [7:0] A,
  output OFL,
  output [7:0] out_3
);

  wire adder_1_cout, or_1_out;

  // Probe on A
  // Probe on {A[5:0], 2'b00}
  or or_1 (or_1_out, A[6], A[7]);
  Adder adder_1 (.a({A[5:0], 2'b00}), .b(A), .out(out_3), .cout(adder_1_cout));  // open: cin
  // Probe on out_3
  or or_2 (OFL, or_1_out, adder_1_cout);
endmodule
