// Logisim project NSU-2023-T05L2e04.circ as structural Verilog: 1 circuit, main circuit mult4x4
module mult4x4 (
  input  [3:0] A,
  input  [3:0] B,
  output [7:0] R
);

  wire [3:0] and_1_out, and_2_out, and_3_out, and_4_out;
  wire [7:0] sum8_1_out, sum8_2_out;

  // Probe on B
  // Probe on A
  assign and_1_out = A & {4{B[0]}};  // AND_Gate and_1, 4 bits wide
  assign and_2_out = A & {4{B[1]}};  // AND_Gate and_2, 4 bits wide
  Sum8 sum8_1 (
    .Out(sum8_1_out), .in1({4'b0000, and_1_out}), .in2({3'b000, and_2_out, 1'b0}), .Cin(1'b0));  // open: Cout
  assign and_3_out = A & {4{B[2]}};  // AND_Gate and_3, 4 bits wide
  Sum8 sum8_2 (.Out(sum8_2_out), .in1(sum8_1_out), .in2({2'b00, and_3_out, 2'b00}), .Cin(1'b0));  // open: Cout
  assign and_4_out = A & {4{B[3]}};  // AND_Gate and_4, 4 bits wide
  // Probe on R
  Sum8 sum8_3 (.Out(R), .in1(sum8_2_out), .in2({1'b0, and_4_out, 3'b000}), .Cin(1'b0));  // open: Cout
endmodule
