// Logisim project NSU-2023-T05L3e02.circ as structural Verilog: 1 circuit, main circuit cmp
module cmp (
  input  [7:0] A,
  input  [7:0] B,
  output Eq,
  output Gt
);

  wire and_1_out, and_2_out, and_3_out, and_4_out, and_5_out, and_6_out, and_7_out, and_8_out, or_1_out,
       or_2_out, or_3_out, or_4_out, or_5_out, or_6_out;
  wire [7:0] xnor_1_out;

  assign xnor_1_out = ~(A ^ B);  // XNOR_Gate xnor_1, 8 bits wide
  and and_1 (and_1_out, ~A[0], B[0]);  // AND_Gate
  and and_2 (and_2_out, ~A[1], B[1]);  // AND_Gate
  and and_3 (and_3_out, ~A[2], B[2]);  // AND_Gate
  and and_4 (and_4_out, ~A[3], B[3]);  // AND_Gate
  and and_5 (and_5_out, ~A[4], B[4]);  // AND_Gate
  and and_6 (and_6_out, ~A[5], B[5]);  // AND_Gate
  and and_7 (and_7_out, ~A[6], B[6]);  // AND_Gate
  and and_8 (and_8_out, ~A[7], B[7]);  // AND_Gate
  and and_9 (Eq, xnor_1_out[0], xnor_1_out[1], xnor_1_out[2], xnor_1_out[3], xnor_1_out[4], xnor_1_out[5], xnor_1_out[6], xnor_1_out[7]);
  or or_1 (or_1_out, and_6_out, or_2_out);
  or or_2 (or_2_out, and_7_out, and_8_out);
  or or_3 (or_3_out, and_3_out, or_4_out);
  or or_4 (or_4_out, and_4_out, or_5_out);
  or or_5 (or_5_out, and_5_out, or_1_out);
  nor nor_1 (Gt, and_1_out, Eq, or_6_out);
  or or_6 (or_6_out, and_2_out, or_3_out);

  // Notes on the sheet:
  //   A: pull=up
endmodule
