// Logisim project NSU-2023-T06L1e02.circ as structural Verilog: 2 circuits, main circuit solution
module solution (
  input  [7:0] A,
  input  set,
  input  [7:0] B,
  input  clock,
  output [7:0] GCD,
  output done
);

  wire buffer_1_out, buffer_2_out, comparator_1_lt, not_1_out, not_2_out, transistor_3_out;
  wire [7:0] adder_1_out, multiplexer_1_out, multiplexer_2_out, negator_1_out, register_1_q, register_2_q,
       transistor_2_out, transistor_4_out;

  // Probe on A
  buf buffer_1 (buffer_1_out, set);
  buf buffer_2 (buffer_2_out, set);
  // Probe on B
  Transistor #(.\type ("n"), .gate("br"), .width(8)) transistor_1 (.in(register_1_q), .out(GCD), .gate(done));
  Transistor #(.gate("br"), .width(8)) transistor_2 (.in(A), .out(transistor_2_out), .gate(buffer_1_out));
  Register register_1 (.D(transistor_2_out), .Q(register_1_q), .clk(transistor_3_out));  // open: en, clr
  Transistor #(.gate("br")) transistor_3 (.in(set), .out(transistor_3_out), .gate(buffer_2_out));
  Transistor #(.width(8)) transistor_4 (.in(B), .out(transistor_4_out), .gate(buffer_2_out));
  Register register_2 (.D(transistor_4_out), .Q(register_2_q), .clk(transistor_3_out));  // open: en, clr
  Transistor #(.width(8)) transistor_5 (.in(adder_1_out), .out(transistor_2_out), .gate(comparator_1_lt));
  Transistor #(.\type ("n"), .gate("br"), .width(8)) transistor_6 (
    .in(adder_1_out), .out(transistor_4_out), .gate(comparator_1_lt));
  Transistor #(.\type ("n")) transistor_7 (.in(clock), .out(transistor_3_out), .gate(buffer_2_out));
  // Probe on GCD
  Comparator comparator_1 (.a(register_1_q), .b(register_2_q), .eq(done), .lt(comparator_1_lt));  // open: gt
  Multiplexer #(.width(8)) multiplexer_1 (
    .in0(register_2_q), .in1(register_1_q), .out(multiplexer_1_out), .sel(not_1_out), .en(not_2_out));
  not not_1 (not_1_out, comparator_1_lt);
  Multiplexer #(.width(8)) multiplexer_2 (
    .in0(register_1_q), .in1(register_2_q), .out(multiplexer_2_out), .sel(not_1_out), .en(not_2_out));
  not not_2 (not_2_out, done);
  Negator negator_1 (.in(multiplexer_2_out), .out(negator_1_out));
  Adder adder_1 (.a(multiplexer_1_out), .b(negator_1_out), .out(adder_1_out));  // open: cin, cout
endmodule

module stopper (
  input  run_prime,
  input  stop,
  input  clock_in,
  output clock_out
);

  wire multiplexer_1_out, not_1_out, or_1_out, register_1_q;

  not not_1 (not_1_out, stop);
  Multiplexer #(.enable("false")) multiplexer_1 (
    .in0(not_1_out), .in1(run_prime), .out(multiplexer_1_out), .sel(run_prime));
  or or_1 (or_1_out, run_prime, register_1_q);
  Register #(.width(1), .trigger("falling")) register_1 (
    .D(multiplexer_1_out), .en(or_1_out), .Q(register_1_q), .clk(clock_in));  // open: clr
  and and_1 (clock_out, register_1_q, clock_in);
endmodule
